// Logisim project apple-pie-cpu.circ as structural Verilog
// Operand Register
module _8Bit_Computer (
  input  HLT,
  input  SEL,
  input  X_In,
  input  X_Out,
  input  Y_In,
  input  Y_Out,
  input  SP_Inc,
  input  SP_Out,
  input  PR_Inc,
  input  PR_JMP,
  input  PC_Inc,
  input  PC_JMP,
  input  SP_Dec,
  input  PR_Out,
  input  PC_Out,
  input  AND,
  input  SUB,
  input  NOT,
  input  OR,
  input  A_Out,
  input  A_In,
  input  B_Out,
  input  B_In,
  input  ALU_Out,
  input  Op2_In,
  input  C_Out,
  input  C_In,
  input  D_Out,
  input  D_In,
  input  Output_In,
  output [15:0] Address_Bus,
  output [15:0] out_32,
  output [15:0] out_33,
  output [7:0] out_34,
  output [7:0] out_35,
  output [7:0] out_36,
  output Cout,
  output Cout_2,
  output Cout_3,
  output [7:0] out_40,
  output [7:0] out_41,
  output [7:0] out_42,
  output [7:0] Op2,
  output [7:0] out_44,
  output [7:0] out_45,
  output [7:0] out_46
);

  wire Clock_clock, CLR_out, MAN_out;
  wire [7:0] pull_resistor_1_node;
  wire [11:0] output_decimal_register_1_hundreds, output_decimal_register_1_hundreds_2;
  wire [15:0] X_Register_to_bus;

  _8bit_register Instruction_Register ();  // open: Register_Out, From_Bus, Register_In, Clock, Clear, To_Bus, Monitor
  sequencer Sequencer ();
  RAM #(.addrWidth(16), .bus("separate")) ram_1 ();  // open: addr, din, data, str, sel, clk, ld, clr
  _8bit_register Memory_Bank_Register ();  // open: Register_Out, From_Bus, Register_In, Clock, Clear, To_Bus, Monitor
  _16bit_register Memory_Access_Register ();  // open: From_Bus, Register_In, Clock, Clear, To_Bus, Monitor, Register_Out
  _8bit_register Operand_Register ();  // open: Register_Out, From_Bus, Register_In, Clock, Clear, To_Bus, Monitor
  instruction_decoder Instruction_Decoder ();
  ROM #(.addrWidth(16)) rom_1 ();  // open: addr, data, sel
  ROM #(.addrWidth(16)) rom_2 ();  // open: addr, data, sel
  Button CLR (.out(CLR_out));
  Button MAN (.out(MAN_out));
  clock Clock (.Select(SEL), .Manual(MAN_out), .Halt(HLT), .Clock(Clock_clock));
  // Probe on pull_resistor_1_node
  Pull_Resistor pull_resistor_1 (.node(pull_resistor_1_node));
  _16bit_register X_Register (
    .From_Bus(Address_Bus), .Register_In(X_In), .Clock(Clock_clock), .Clear(CLR_out),
    .To_Bus(X_Register_to_bus), .Monitor(out_32), .Register_Out(X_Out));
  _8bit_register A_Register (
    .Register_Out(A_Out), .From_Bus(pull_resistor_1_node), .Register_In(A_In), .Clock(Clock_clock),
    .Clear(CLR_out), .To_Bus(pull_resistor_1_node), .Monitor(out_40));
  _8bit_register C_Register (
    .Register_Out(C_Out), .From_Bus(pull_resistor_1_node), .Register_In(C_In), .Clock(Clock_clock),
    .Clear(CLR_out), .To_Bus(pull_resistor_1_node), .Monitor(out_44));
  output_decimal_register output_decimal_register_1 (
    .From_Bus(pull_resistor_1_node), .Output_In(Output_In), .CLK(Clock_clock), .CLR(CLR_out),
    .Monitor(out_46), .Hundreds({output_decimal_register_1_hundreds_2, output_decimal_register_1_hundreds}));
  stack_pointer stack_pointer_1 (
    .Monitor(out_34), .To_Bus(pull_resistor_1_node), .INC(SP_Inc), .CLK(Clock_clock), .CLR(CLR_out),
    .Cout(Cout), .Counter_Out(SP_Out), .DEC(SP_Dec));
  _7_Segment_Display u_7_segment_display_1 (
    .g(output_decimal_register_1_hundreds[7]), .f(output_decimal_register_1_hundreds[6]),
    .a(output_decimal_register_1_hundreds[5]), .b(output_decimal_register_1_hundreds[4]),
    .e(output_decimal_register_1_hundreds_2[7]), .d(output_decimal_register_1_hundreds_2[6]),
    .c(output_decimal_register_1_hundreds_2[5]), .dp(output_decimal_register_1_hundreds_2[4]));
  _7_Segment_Display u_7_segment_display_2 (
    .g(output_decimal_register_1_hundreds[11]), .f(output_decimal_register_1_hundreds[10]),
    .a(output_decimal_register_1_hundreds[9]), .b(output_decimal_register_1_hundreds[8]),
    .e(output_decimal_register_1_hundreds_2[11]), .d(output_decimal_register_1_hundreds_2[10]),
    .c(output_decimal_register_1_hundreds_2[9]), .dp(output_decimal_register_1_hundreds_2[8]));
  _8bit_counter Page_Register (
    .From_Bus(pull_resistor_1_node), .Monitor(out_35), .To_Bus(pull_resistor_1_node), .JMP(PR_JMP),
    .INC(PR_Inc), .CLK(Clock_clock), .CLR(CLR_out), .Cout(Cout_2), .Counter_Out(PR_Out));
  _8bit_register B_Register (
    .Register_Out(B_Out), .From_Bus(pull_resistor_1_node), .Register_In(B_In), .Clock(Clock_clock),
    .Clear(CLR_out), .To_Bus(pull_resistor_1_node), .Monitor(out_41));
  _8bit_register D_Register (
    .Register_Out(D_Out), .From_Bus(pull_resistor_1_node), .Register_In(D_In), .Clock(Clock_clock),
    .Clear(CLR_out), .To_Bus(pull_resistor_1_node), .Monitor(out_45));
  _7_Segment_Display u_7_segment_display_3 (
    .g(output_decimal_register_1_hundreds[3]), .f(output_decimal_register_1_hundreds[2]),
    .a(output_decimal_register_1_hundreds[1]), .b(output_decimal_register_1_hundreds[0]),
    .e(output_decimal_register_1_hundreds_2[3]), .d(output_decimal_register_1_hundreds_2[2]),
    .c(output_decimal_register_1_hundreds_2[1]), .dp(output_decimal_register_1_hundreds_2[0]));
  _16bit_register Y_Register (
    .From_Bus(Address_Bus), .Register_In(Y_In), .Clock(Clock_clock), .Clear(CLR_out),
    .To_Bus(X_Register_to_bus), .Monitor(Address_Bus), .Register_Out(Y_Out));
  alu_1 ALU (
    .ALU_Output(ALU_Out), .Input_A(out_40), .SUB(SUB), .NOT(NOT), .AND(AND), .OR(OR),
    .To_Bus(pull_resistor_1_node), .Monitor(out_42), .From_Bus(pull_resistor_1_node), .Register_In(Op2_In),
    .Input_B(Op2), .Clock(Clock_clock), .Clear(CLR_out));
  _8bit_counter Program_Counter (
    .From_Bus(pull_resistor_1_node), .Monitor(out_36), .To_Bus(pull_resistor_1_node), .JMP(PC_JMP),
    .INC(PC_Inc), .CLK(Clock_clock), .CLR(CLR_out), .Cout(Cout_3), .Counter_Out(PC_Out));
  Pull_Resistor pull_resistor_2 (.node(Address_Bus));

  assign out_33 = Address_Bus;
endmodule

module clock (
  input  Select,
  input  Manual,
  input  Halt,
  output Clock
);

  wire and_1_out, and_2_out, clock_1_out, not_1_out, not_2_out, or_1_out;

  Clock clock_1 (.out(clock_1_out));
  and and_1 (and_1_out, clock_1_out, Select);
  not not_1 (not_1_out, Select);
  and and_2 (and_2_out, not_1_out, Manual);
  not not_2 (not_2_out, Halt);
  or or_1 (or_1_out, and_1_out, and_2_out);
  and and_3 (Clock, or_1_out, not_2_out);
endmodule

module _8bit_register (
  input  Register_Out,
  input  [7:0] From_Bus,
  input  Register_In,
  input  Clock,
  input  Clear,
  output [7:0] To_Bus,
  output [7:0] Monitor
);

  Pull_Resistor pull_resistor_1 (.node(Register_In));
  Pull_Resistor pull_resistor_2 (.node(Clock));
  Pull_Resistor pull_resistor_3 (.node(Clear));
  Register register_1 (.D(From_Bus), .en(Register_In), .Q(Monitor), .clk(Clock), .clr(Clear));
  Pull_Resistor pull_resistor_4 (.node(Register_Out));
  assign To_Bus = Register_Out ? Monitor : 8'bz;  // Controlled_Buffer controlled_buffer_1
endmodule

module _16bit_register (
  input  Register_Out,
  input  [15:0] From_Bus,
  input  Register_In,
  input  Clock,
  input  Clear,
  output [15:0] To_Bus,
  output [15:0] Monitor
);

  Pull_Resistor pull_resistor_1 (.node(Register_In));
  Pull_Resistor pull_resistor_2 (.node(Clock));
  Pull_Resistor pull_resistor_3 (.node(Clear));
  Register #(.width(16)) register_1 (.D(From_Bus), .en(Register_In), .Q(Monitor), .clk(Clock), .clr(Clear));
  Pull_Resistor pull_resistor_4 (.node(Register_Out));
  assign To_Bus = Register_Out ? Monitor : 16'bz;  // Controlled_Buffer controlled_buffer_1
endmodule

module alu_0 (
  input  ALU_Output,
  input  [7:0] A_Input,
  input  SUB,
  input  NOT,
  input  AND,
  input  OR,
  input  [7:0] B_Input,
  output [7:0] Monitor,
  output [7:0] To_Bus
);

  wire or_1_out, or_2_out, xor_1_out;
  wire [7:0] adder_1_out, and_1_out, bit_extender_1_out, multiplexer_1_out, or_3_out, xor_2_out;

  or or_1 (or_1_out, SUB, NOT);
  or or_2 (or_2_out, AND, OR);
  assign bit_extender_1_out = {{7{or_1_out}}, or_1_out};  // Bit_Extender bit_extender_1
  xor xor_1 (xor_1_out, or_1_out, NOT);
  assign xor_2_out = bit_extender_1_out ^ B_Input;  // XOR_Gate xor_2, 8 bits wide
  Adder adder_1 (.a(A_Input), .b(xor_2_out), .out(adder_1_out), .cin(xor_1_out));  // open: cout
  assign and_1_out = A_Input & B_Input;  // AND_Gate and_1, 8 bits wide
  Multiplexer #(.width(8), .enable("false")) multiplexer_1 (
    .in0(and_1_out), .in1(or_3_out), .out(multiplexer_1_out), .sel(OR));
  assign or_3_out = A_Input | B_Input;  // OR_Gate or_3, 8 bits wide
  Multiplexer #(.width(8), .enable("false")) multiplexer_2 (
    .in0(adder_1_out), .in1(multiplexer_1_out), .out(Monitor), .sel(or_2_out));
  assign To_Bus = ALU_Output ? Monitor : 8'bz;  // Controlled_Buffer controlled_buffer_1
endmodule

module stack_pointer (
  input  DEC,
  input  INC,
  input  CLK,
  input  CLR,
  input  Counter_Out,
  output [7:0] Monitor,
  output [7:0] To_Bus,
  output Cout
);

  wire xor_1_out;
  wire [7:0] pull_resistor_3_node;

  Pull_Resistor pull_resistor_1 (.node(DEC));
  xor xor_1 (xor_1_out, DEC, INC);
  Pull_Resistor pull_resistor_2 (.node(INC));
  Pull_Resistor pull_resistor_3 (.node(pull_resistor_3_node));
  Counter counter_1 (
    .load(DEC), .D(pull_resistor_3_node), .count(xor_1_out), .Q(Monitor), .carry(Cout), .clk(CLK), .clr(CLR));
  Pull_Resistor pull_resistor_4 (.node(CLR));
  Pull_Resistor pull_resistor_5 (.node(CLK));
  Pull_Resistor pull_resistor_6 (.node(Cout));
  assign To_Bus = Counter_Out ? Monitor : 8'bz;  // Controlled_Buffer controlled_buffer_1
  Pull_Resistor pull_resistor_7 (.node(Counter_Out));
endmodule

module _8bit_counter (
  input  [7:0] From_Bus,
  input  JMP,
  input  INC,
  input  CLK,
  input  CLR,
  input  Counter_Out,
  output [7:0] Monitor,
  output [7:0] To_Bus,
  output Cout
);

  wire [7:0] controlled_buffer_1_out;

  Pull_Resistor pull_resistor_1 (.node(JMP));
  Pull_Resistor pull_resistor_2 (.node(INC));
  Pull_Resistor pull_resistor_3 (.node(CLK));
  assign controlled_buffer_1_out = JMP ? From_Bus : 8'bz;  // Controlled_Buffer controlled_buffer_1
  Counter counter_1 (
    .load(JMP), .D(controlled_buffer_1_out), .count(INC), .Q(Monitor), .carry(Cout), .clk(CLK), .clr(CLR));
  Pull_Resistor pull_resistor_4 (.node(Cout));
  Pull_Resistor pull_resistor_5 (.node(CLR));
  assign To_Bus = Counter_Out ? Monitor : 8'bz;  // Controlled_Buffer controlled_buffer_2
  Pull_Resistor pull_resistor_6 (.node(Counter_Out));
endmodule

module output_decimal_register (
  input  [7:0] From_Bus,
  input  Output_In,
  input  CLK,
  input  CLR,
  output [7:0] Monitor,
  output [23:0] Hundreds
);

  wire pull_resistor_4_node;

  Register register_1 (.D(From_Bus), .en(Output_In), .Q(Monitor), .clk(CLK), .clr(CLR));
  Pull_Resistor pull_resistor_1 (.node(Output_In));
  Pull_Resistor pull_resistor_2 (.node(CLK));
  Pull_Resistor pull_resistor_3 (.node(CLR));
  Pull_Resistor #(.pull(1)) pull_resistor_4 (.node(pull_resistor_4_node));
  ROM #(.dataWidth(24)) rom_1 (.addr(Monitor), .data(Hundreds), .sel(pull_resistor_4_node));

  // Notes on the sheet:
  //   contents of rom_1 (hex, n*v repeats v):
  //   e007 2001 c00b 600b 200d 600e e00e 2003 e00f 200f 2e017 22011 2c01b 2601b 2201d 2601e 2e01e 22013
  //   2e01f 2201f ce0b7 c20b1 cc0bb c60bb c20bd c60be ce0be c20b3 ce0bf c20bf 6e0b7 620b1 6c0bb 660bb
  //   620bd 660be 6e0be 620b3 6e0bf 620bf 2e0d7 220d1 2c0db 260db 220dd 260de 2e0de 220d3 2e0df 220df
  //   6e0e7 620e1 6c0eb 660eb 620ed 660ee 6e0ee 620e3 6e0ef 620ef ee0e7 e20e1 ec0eb e60eb e20ed e60ee
  //   ee0ee e20e3 ee0ef e20ef 2e037 22031 2c03b 2603b 2203d 2603e 2e03e 22033 2e03f 2203f ee0f7 e20f1
  //   ec0fb e60fb e20fd e60fe ee0fe e20f3 ee0ff e20ff 2e0f7 220f1 2c0fb 260fb 220fd 260fe 2e0fe 220f3
  //   2e0ff 220ff 2ee177 2e2171 2ec17b 2e617b 2e217d 2e617e 2ee17e 2e2173 2ee17f 2e217f 22e117 222111
  //   22c11b 22611b 22211d 22611e 22e11e 222113 22e11f 22211f 2ce1b7 2c21b1 2cc1bb 2c61bb 2c21bd 2c61be
  //   2ce1be 2c21b3 2ce1bf 2c21bf 26e1b7 2621b1 26c1bb 2661bb 2621bd 2661be 26e1be 2621b3 26e1bf 2621bf
  //   22e1d7 2221d1 22c1db 2261db 2221dd 2261de 22e1de 2221d3 22e1df 2221df 26e1e7 2621e1 26c1eb 2661eb
  //   2621ed 2661ee 26e1ee 2621e3 26e1ef 2621ef 2ee1e7 2e21e1 2ec1eb 2e61eb 2e21ed 2e61ee 2ee1ee 2e21e3
  //   2ee1ef 2e21ef 22e137 222131 22c13b 22613b 22213d 22613e 22e13e 222133 22e13f 22213f 2ee1f7 2e21f1
  //   2ec1fb 2e61fb 2e21fd 2e61fe 2ee1fe 2e21f3 2ee1ff 2e21ff 22e1f7 2221f1 22c1fb 2261fb 2221fd 2261fe
  //   22e1fe 2221f3 22e1ff 2221ff ceeb77 ce2b71 cecb7b ce6b7b ce2b7d ce6b7e ceeb7e ce2b73 ceeb7f ce2b7f
  //   c2eb17 c22b11 c2cb1b c26b1b c22b1d c26b1e c2eb1e c22b13 c2eb1f c22b1f ccebb7 cc2bb1 cccbbb cc6bbb
  //   cc2bbd cc6bbe ccebbe cc2bb3 ccebbf cc2bbf c6ebb7 c62bb1 c6cbbb c66bbb c62bbd c66bbe c6ebbe c62bb3
  //   c6ebbf c62bbf c2ebd7 c22bd1 c2cbdb c26bdb c22bdd c26bde c2ebde c22bd3 c2ebdf c22bdf c6ebe7 c62be1
  //   c6cbeb c66beb c62bed c66bee
endmodule

module alu_1 (
  input  ALU_Output,
  input  [7:0] Input_A,
  input  SUB,
  input  NOT,
  input  AND,
  input  OR,
  input  [7:0] From_Bus,
  input  Register_In,
  input  Clock,
  input  Clear,
  output [7:0] Monitor,
  output [7:0] To_Bus,
  output [7:0] Input_B
);

  wire or_1_out, or_2_out, xor_1_out;
  wire [7:0] adder_1_out, and_1_out, bit_extender_1_out, multiplexer_1_out, multiplexer_2_out, or_3_out,
       xor_2_out;

  Pull_Resistor pull_resistor_1 (.node(SUB));
  Pull_Resistor pull_resistor_2 (.node(NOT));
  Pull_Resistor pull_resistor_3 (.node(AND));
  Pull_Resistor pull_resistor_4 (.node(OR));
  Pull_Resistor pull_resistor_5 (.node(Register_In));
  Pull_Resistor pull_resistor_6 (.node(Clock));
  Pull_Resistor pull_resistor_7 (.node(Clear));
  Register register_1 (.D(From_Bus), .en(Register_In), .Q(Input_B), .clk(Clock), .clr(Clear));
  or or_1 (or_1_out, AND, OR);
  or or_2 (or_2_out, SUB, NOT);
  assign bit_extender_1_out = {{7{or_2_out}}, or_2_out};  // Bit_Extender bit_extender_1
  xor xor_1 (xor_1_out, or_2_out, NOT);
  assign xor_2_out = bit_extender_1_out ^ Input_B;  // XOR_Gate xor_2, 8 bits wide
  Multiplexer #(.width(8), .enable("false")) multiplexer_1 (
    .in0(Input_A), .in1({8{1'b0}}), .out(multiplexer_1_out), .sel(NOT));
  assign and_1_out = Input_A & Input_B;  // AND_Gate and_1, 8 bits wide
  assign or_3_out = Input_A | Input_B;  // OR_Gate or_3, 8 bits wide
  Adder adder_1 (.a(multiplexer_1_out), .b(xor_2_out), .out(adder_1_out), .cin(xor_1_out));  // open: cout
  Multiplexer #(.width(8), .enable("false")) multiplexer_2 (
    .in0(and_1_out), .in1(or_3_out), .out(multiplexer_2_out), .sel(OR));
  Multiplexer #(.width(8), .enable("false")) multiplexer_3 (
    .in0(adder_1_out), .in1(multiplexer_2_out), .out(Monitor), .sel(or_1_out));
  assign To_Bus = ALU_Output ? Monitor : 8'bz;  // Controlled_Buffer controlled_buffer_1
endmodule

module alu_2 (
  input  NOT,
  input  SUB,
  input  [7:0] INPUT_A,
  input  [7:0] From_Bus,
  input  Register_In,
  input  AND,
  input  Clock,
  input  OR,
  input  Clear,
  input  LSL,
  input  LSR,
  input  ALU_Output,
  input  Update_Flags,
  output [7:0] To_Bus,
  output [7:0] Output,
  output [7:0] INPUT_B
);

  wire nor_1_out, not_1_out, or_2_out;
  wire [2:0] bit_extender_2_out;
  wire [3:0] nor_2_out;
  wire [7:0] adder_1_out, and_1_out, bit_extender_1_out, multiplexer_1_out, multiplexer_2_out,
       multiplexer_3_out, multiplexer_4_out, not_2_out, or_1_out, shifter_1_out, shifter_2_out, xor_1_out;

  Register register_1 (.D(From_Bus), .en(Register_In), .Q(INPUT_B), .clk(Clock), .clr(Clear));
  assign bit_extender_1_out = {{7{SUB}}, SUB};  // Bit_Extender bit_extender_1
  Bit_Extender #(.out_width(3)) bit_extender_2 (.in(INPUT_B), .out(bit_extender_2_out));
  not not_1 (not_1_out, NOT);
  assign not_2_out = ~INPUT_A;  // NOT_Gate not_2, 8 bits wide
  Shifter shifter_1 (.in(INPUT_A), .\dist (bit_extender_2_out), .out(shifter_1_out));
  Shifter #(.shift("lr")) shifter_2 (.in(INPUT_A), .\dist (bit_extender_2_out), .out(shifter_2_out));
  assign xor_1_out = bit_extender_1_out ^ INPUT_B;  // XOR_Gate xor_1, 8 bits wide
  assign and_1_out = INPUT_A & INPUT_B;  // AND_Gate and_1, 8 bits wide
  assign or_1_out = INPUT_A | INPUT_B;  // OR_Gate or_1, 8 bits wide
  or or_2 (or_2_out, AND, OR);
  nor nor_1 (nor_1_out, LSL, LSR);
  Multiplexer #(.width(8), .enable("false")) multiplexer_1 (
    .in0(shifter_1_out), .in1(shifter_2_out), .out(multiplexer_1_out), .sel(LSR));
  Adder adder_1 (.a(INPUT_A), .b(xor_1_out), .out(adder_1_out), .cin(SUB), .cout(nor_2_out[2]));
  Multiplexer #(.width(8), .enable("false")) multiplexer_2 (
    .in0(not_2_out), .in1(adder_1_out), .out(multiplexer_2_out), .sel(not_1_out));
  Multiplexer #(.width(8), .enable("false")) multiplexer_3 (
    .in0(and_1_out), .in1(or_1_out), .out(multiplexer_3_out), .sel(OR));
  Multiplexer #(.width(8), .enable("false")) multiplexer_4 (
    .in0(multiplexer_2_out), .in1(multiplexer_3_out), .out(multiplexer_4_out), .sel(or_2_out));
  Multiplexer #(.width(8), .enable("false")) multiplexer_5 (
    .in0(multiplexer_1_out), .in1(multiplexer_4_out), .out(Output), .sel(nor_1_out));
  assign To_Bus = ALU_Output ? Output : 8'bz;  // Controlled_Buffer controlled_buffer_1
  nor nor_2 (nor_2_out[0], Output[0], Output[1], Output[2], Output[3], Output[4], Output[5], Output[6], Output[7]);
  Register #(.width(4)) register_2 (.D(nor_2_out), .en(Update_Flags), .clk(Clock), .clr(Clear));  // open: Q
endmodule

module address_fun (
  input  [3:0] in_1,
  output out_2,
  output out_3,
  output out_4,
  output out_5,
  output out_6,
  output out_7,
  output out_8,
  output out_9,
  output out_10,
  output out_11,
  output out_12,
  output out_13,
  output out_14,
  output out_15,
  output out_16,
  output out_17,
  output out_18
);

  Decoder #(.select(4), .enable("false")) decoder_1 (
    .out0(out_2), .out1(out_3), .out2(out_4), .out3(out_5), .out4(out_6), .out5(out_7), .out6(out_8),
    .out7(out_9), .out8(out_11), .out9(out_12), .out10(out_13), .out11(out_14), .out12(out_15),
    .out13(out_16), .out14(out_17), .out15(out_18), .sel(in_1));

  // Notes on the sheet:
  //   Bank Register Select Line (4 bit)
endmodule
