// Digital circuit BW8comp.dig as structural Verilog
module BW8comp (
  input  crystal,
  input  _555,
  input  step,
  output [15:0] addr,
  output [7:0] data,
  output r_nw,
  output nack
);

  wire clk_cpu, clk_crystal, nbrk;
  wire [0:0] rst_clk_mode;
  wire [2:0] Break_out, triple_clock_1_p9;

  Button #(.activeLow("true")) Run (.out(Break_out[0]));
  Button #(.activeLow("true")) Demo (.out(Break_out[1]));
  Button #(.activeLow("true")) Break (.out(Break_out[2]));
  Reset Power_On_Reset (.out(rst_clk_mode[0]));
  BW8cpu bw8cpu_1 (
    .VCC(1'b1), .GND(1'b0), .nRST(1'b1), .nIRQ(1'b1), .nREQ(clk_cpu), .CLK(rst_clk_mode[0]), .ADDR(addr),
    .DATA(data), .R_nW(r_nw), .nACK(nack), .nBRK(nbrk));  // open: DBG
  // triple_clock triple_clock_1: pin names not known; wires that end beside it: {2'b11, rst_clk_mode[0]}, nbrk, Break_out, crystal, _555, step, clk_cpu, clk_crystal, triple_clock_1_p9
  LED u_crystal (.in(clk_crystal));
  LED cpu (.in(clk_cpu));
  LED Run_Mode_Active (.in(triple_clock_1_p9[0]));
  LED Demo_Mode_Active (.in(triple_clock_1_p9[1]));
  LED Break_Mode_Active (.in(triple_clock_1_p9[2]));

  // Notes on the sheet:
  //   crystal: Hz: 5
endmodule
