// Digital circuit BW8cpu.dig as structural Verilog
module BW8cpu (
  input  crystal,
  input  _555,
  input  VCC,
  input  GND,
  input  nREQ,
  input  nNMI,
  input  nIRQ,
  input  step,
  output halt,
  output nACK,
  output D_nC,
  output MEM_nIO,
  output R_nW,
  output [7:0] DATA,
  output [19:0] ADDR,
  output U_nS,
  output \assert 
);

  wire a_dbus_a, a_dbus_l, a_lhs_a, a_rhs_a, addr_a, addr_inc, addr_xfer_a, alu_dbus_a, b_dbus_a, b_dbus_l,
       b_lhs_a, b_rhs_a, br_dbus_a, br_dbus_l, button_1_out, c_dbus_a, c_dbus_l, c_f, c_lhs_a, c_rhs_a, clk,
       clk_crystal, clr_ubr, count, d_dbus_a, d_dbus_l, d_lhs_a, d_rhs_a, da_dbus_a, da_dbus_l, dbus_a,
       dbus_l, dec_sp, dp_addr_a, dp_dbus_a, dp_dbus_l, ext, io_addr_a, ir_dbus_l, isr_xfer_a, lsb_dbus_a,
       mem_dbus_a, mem_dbus_l, msb_dbus_a, musteq_load, nclk, noffset, not_2_out, not_3_out, nrst, nRST_out,
       oe, off_dbus_l, pc_addr_a, pc_inc, pc_xfer_a, pc_xfer_l, pch_dbus_l, pcl_dbus_l, ram_cs, reset_1_out,
       rom_cs, rst, set_nmi_inh, set_sup, set_ubr, sp_addr_a, sp_dec, sp_inc, sp_xfer_a, sp_xfer_l,
       sph_dbus_l, spl_dbus_l, sr_dbus_a, sr_dbus_l, step_t, t_addr_a, th_dbus_a, th_dbus_l, th_lhs_a,
       tl_dbus_a, tl_dbus_l, tl_rhs_a, we, x_addr_a, x_dec, x_inc, x_xfer_a, x_xfer_l, xfer_a, xfer_l,
       xh_dbus_l, xl_dbus_l, y_addr_a, y_dec, y_inc, y_xfer_a, y_xfer_l, yh_dbus_l, yl_dbus_l;
  wire [1:0] Control_Unit_p22_2;
  wire [2:0] Break_out, clk_mode, t_state;
  wire [3:0] alu_op;
  wire [7:0] alu_res, dbus, flags, lhs, opcode, reg_a, reg_b, reg_c, reg_d, reg_da, reg_dp, reg_off, reg_th,
       reg_tl, rhs;
  wire [14:3] Control_Unit_p22;
  wire [15:0] addr_t, reg_pc, reg_sp, reg_x, reg_y;

  LED led_1 (.in(clk));
  LED led_2 (.in(nrst));
  // Probe on dbus
  // Probe on {lhs, rhs}
  // Probe on ADDR
  // Probe NMIIf on flags[7]
  // Probe UBRf on flags[6]
  // Probe USf on U_nS
  // Probe Cf on c_f
  // Probe Zf on flags[3]
  // Probe Vf on flags[2]
  // Probe Nf on flags[1]
  // Probe If on flags[0]
  // Probe IR on opcode
  // Probe on t_state
  PowerSupply powersupply_1 (.VDD(VCC), .GND(GND));
  PullUp pullup_1 (.out(R_nW));
  PullUp pullup_2 (.out(MEM_nIO));
  PullDown #(.Bits(20)) pulldown_1 (.out(ADDR));
  PullDown #(.Bits(8)) pulldown_2 (.out(DATA));
  PullUp pullup_3 (.out(D_nC));
  // Probe on addr_t
  // Probe on DATA
  // Probe PC on reg_pc
  // Probe SP on reg_sp
  // Probe X on reg_x
  // Probe Y on reg_y
  // Probe A on reg_a
  // Probe B on reg_b
  // Probe C on reg_c
  // Probe D on reg_d
  // Probe DP on reg_dp
  // Probe DA on reg_da
  // Probe TL on reg_tl
  // Probe TH on reg_th
  // Probe OFF on reg_off
  // Probe on alu_res
  // Probe on opcode
  // Probe on ext
  Button #(.activeLow("true")) Run (.out(Break_out[0]));
  Button #(.activeLow("true")) Demo (.out(Break_out[1]));
  Button #(.activeLow("true")) Break (.out(Break_out[2]));
  not not_1 (halt, musteq_load);
  Button button_1 (.out(button_1_out));
  or or_1 (step_t, button_1_out, step);
  // Probe on {flags[7:6], U_nS, c_f, flags[3:0]}
  Reset reset_1 (.out(reset_1_out));
  and and_1 (nrst, reset_1_out, nRST_out);
  Button #(.activeLow("true")) u_nRST (.out(nRST_out));
  // Probe on t_state
  memory_bridge Memory_Bridge (.dbus_assert(mem_dbus_a), .dbus_load(mem_dbus_l), .dbus(dbus), .mbus(DATA));
  RAMSinglePortSel #(.AddrBits(15), .Bits(8)) ramsingleportsel_1 (
    .A(ADDR[14:0]), .CS(ram_cs), .WE(we), .OE(oe), .D(DATA));
  // triple_clock triple_clock_1: pin names not known; wires that end beside it: Break_out, musteq_load, {nrst, 2'b11}, crystal, _555, step_t, clk, clk_crystal, clk_mode
  // Probe on nclk
  // Probe on count
  // Probe on dec_sp
  assign dbus = ~msb_dbus_a ? lhs : 8'bz;  // DriverInvSel driverinvsel_1
  assign dbus = ~lsb_dbus_a ? rhs : 8'bz;  // DriverInvSel driverinvsel_2
  ROM #(.AddrBits(15), .isProgramMemory("true"), .Bits(8)) rom_1 (.A(ADDR[14:0]), .sel(rom_cs), .D(DATA));
  LED u_crystal (.in(clk_crystal));
  LED cpu (.in(clk));
  LED Run_Mode_Active (.in(clk_mode[0]));
  LED Demo_Mode_Active (.in(clk_mode[1]));
  LED Break_Mode_Active (.in(clk_mode[2]));
  // Probe on addr_a
  // Probe on xfer_l
  // Probe on xfer_a
  address_register Program_Counter (
    .clk(clk), .clr(rst), .inc(pc_inc), .dec(1'b1), .xfer_load(pc_xfer_l), .addr_assert(pc_addr_a),
    .xfer_assert(pc_xfer_a), .dbus_load_hi(pch_dbus_l), .dbus_load_lo(pcl_dbus_l), .dbus(dbus),
    .addr(addr_t), .xfer({lhs, rhs}), .\reg (reg_pc));
  address_register Stack_Pointer (
    .clk(clk), .clr(rst), .inc(sp_inc), .dec(sp_dec), .xfer_load(sp_xfer_l), .addr_assert(sp_addr_a),
    .xfer_assert(sp_xfer_a), .dbus_load_hi(sph_dbus_l), .dbus_load_lo(spl_dbus_l), .dbus(dbus),
    .addr(addr_t), .xfer({lhs, rhs}), .\reg (reg_sp));
  address_register X_Index (
    .clk(clk), .clr(rst), .inc(x_inc), .dec(x_dec), .xfer_load(x_xfer_l), .addr_assert(x_addr_a),
    .xfer_assert(x_xfer_a), .dbus_load_hi(xh_dbus_l), .dbus_load_lo(xl_dbus_l), .dbus(dbus), .addr(addr_t),
    .xfer({lhs, rhs}), .\reg (reg_x));
  address_register Y_Index (
    .clk(clk), .clr(rst), .inc(y_inc), .dec(y_dec), .xfer_load(y_xfer_l), .addr_assert(y_addr_a),
    .xfer_assert(y_xfer_a), .dbus_load_hi(yh_dbus_l), .dbus_load_lo(yl_dbus_l), .dbus(dbus), .addr(addr_t),
    .xfer({lhs, rhs}), .\reg (reg_y));
  // Probe on alu_op
  // Probe on dbus_l
  // Probe on dbus_a
  dual_reg8 A_and_B (
    .rst(rst), .nclk(nclk), .dbus(dbus), .nload_lhs(a_dbus_l), .nassert_outa_lhs(a_dbus_a),
    .nassert_outb_lhs(a_lhs_a), .nassert_outc_lhs(a_rhs_a), .nload_rhs(b_dbus_l),
    .nassert_outa_rhs(b_dbus_a), .nassert_outb_rhs(b_lhs_a), .nassert_outc_rhs(b_rhs_a), .Q_lhs(reg_a),
    .out_a_lhs(dbus), .out_b_lhs(lhs), .out_c_lhs(rhs), .Q_rhs(reg_b), .out_a_rhs(dbus), .out_b_rhs(lhs),
    .out_c_rhs(rhs));
  dual_reg8 C_and_D (
    .rst(rst), .nclk(nclk), .dbus(dbus), .nload_lhs(c_dbus_l), .nassert_outa_lhs(c_dbus_a),
    .nassert_outb_lhs(c_lhs_a), .nassert_outc_lhs(c_rhs_a), .nload_rhs(d_dbus_l),
    .nassert_outa_rhs(d_dbus_a), .nassert_outb_rhs(d_lhs_a), .nassert_outc_rhs(d_rhs_a), .Q_lhs(reg_c),
    .out_a_lhs(dbus), .out_b_lhs(lhs), .out_c_lhs(dbus), .Q_rhs(reg_d), .out_a_rhs(dbus), .out_b_rhs(lhs),
    .out_c_rhs(rhs));
  dual_reg8 DA_and_DP (
    .rst(rst), .nclk(nclk), .dbus(dbus), .nload_lhs(dp_dbus_l), .nassert_outa_lhs(dp_dbus_a),
    .nassert_outb_lhs(dp_addr_a), .nassert_outc_lhs(1'b0), .nload_rhs(da_dbus_l),
    .nassert_outa_rhs(da_dbus_a), .nassert_outb_rhs(dp_addr_a), .nassert_outc_rhs(1'b0), .Q_lhs(reg_dp),
    .out_a_lhs(dbus), .out_b_lhs(addr_t[15:8]), .Q_rhs(reg_da), .out_a_rhs(dbus), .out_b_rhs(addr_t[7:0]));  // open: out_c_lhs, out_c_rhs
  dual_reg8 TH_and_TL (
    .rst(rst), .nclk(nclk), .dbus(dbus), .nload_lhs(th_dbus_l), .nassert_outa_lhs(th_dbus_a),
    .nassert_outb_lhs(th_lhs_a), .nassert_outc_lhs(t_addr_a), .nload_rhs(tl_dbus_l),
    .nassert_outa_rhs(tl_dbus_a), .nassert_outb_rhs(tl_rhs_a), .nassert_outc_rhs(t_addr_a), .Q_lhs(reg_th),
    .out_a_lhs(dbus), .out_b_lhs(lhs), .out_c_lhs(addr_t[15:8]), .Q_rhs(reg_tl), .out_a_rhs(dbus),
    .out_b_rhs(rhs), .out_c_rhs(addr_t[7:0]));
  addr_decoding addr_decoding_1 (
    .A15(ADDR[15]), .R_nW(R_nW), .nCLK(nclk), .ROM_CS(rom_cs), .RAM_CS(ram_cs), .WE(we), .OE(oe));
  not not_2 (not_2_out, addr_inc);
  not not_3 (not_3_out, nACK);
  alu Arithmetic___Logic_Unit_and_Status_Register (
    .alu_op(alu_op), .load_sr_dbus(sr_dbus_l), .assert_sr_dbus(sr_dbus_a), .clk(nclk), .clr(rst), .lhs(lhs),
    .rhs(rhs), .assert_alu_dbus(alu_dbus_a), .set_nmi_inhib(set_nmi_inh), .clr_ubr(clr_ubr),
    .set_ubr(set_ubr), .set_sup(set_sup), .flags({flags[7:6], U_nS, c_f, flags[3:0]}), .dbus(dbus),
    .q(alu_res));
  // control_unit Control_Unit: pin names not known; wires that end beside it: nIRQ, opcode, {flags[7:6], U_nS, c_f, flags[3:0]}, nREQ, nrst, nNMI, clk, 16'h6, 16'h3, isr_xfer_a, dbus_a, dbus_l, alu_op, xfer_a, xfer_l, addr_a, count, dec_sp, nclk, noffset, rst, {Control_Unit_p22_2, ext, Control_Unit_p22, t_state}, {lhs, rhs}, clr_ubr, set_ubr, set_sup, set_nmi_inh
  address_offset Address_Bridge (
    .dbus(dbus), .addr_in(addr_t), .noffset_en(noffset), .carry_en(not_2_out),
    .naddr_xfer_assert(addr_xfer_a), .nassert_addr(not_3_out), .clr(rst), .noffset_load(off_dbus_l),
    .nclock(nclk), .R_nW(mem_dbus_l), .MEM_nIO(io_addr_a), .D_nC(pc_addr_a), .nACK(nACK),
    .nload_br(br_dbus_l), .nassert_br(br_dbus_a), .U_nS(1'b0), .UBR_f(1'b0), .addr_out(ADDR),
    .xfer({lhs, rhs}), .q(reg_off), .R_nW_z(R_nW), .MEM_nIO_z(MEM_nIO), .D_nC_z(D_nC));
  instruction_register Instruction_Register (
    .dbus(dbus), .ndbus_load(ir_dbus_l), .clr(rst), .nclk(nclk), .opcode(opcode));
  // bus_controller Bus_Controller: pin names not known; wires that end beside it: dbus_a, xfer_l, addr_a, clk, count, dec_sp, nclk, dbus_l, xfer_a, alu_dbus_a, a_dbus_a, b_dbus_a, c_dbus_a, d_dbus_a, dp_dbus_a, da_dbus_a, th_dbus_a, tl_dbus_a, sr_dbus_a, mem_dbus_a, msb_dbus_a, lsb_dbus_a, a_dbus_l, b_dbus_l, c_dbus_l

  assign \assert  = 1'b1;

  // Other names for the same wires on the sheet: ack_addr_a = nACK; aout[19:0] = ADDR; low_15[14:0] = ADDR[14:0];
  //   clk_cpu = clk; d_nc_z = D_nC; i_f = flags[0]; n_f = flags[1]; v_f = flags[2]; z_f = flags[3];
  //   flags[5:4] = {U_nS, c_f}; u_ns_f = U_nS; ubr_f = flags[6]; nmi_i_f = flags[7]; mbus[7:0] = DATA;
  //   mem_nio_z = MEM_nIO; rst_clk_mode[2] = nrst; r_nw_z = R_nW; xfer[15:0] = {lhs, rhs}

  // Notes on the sheet:
  //   crystal: Hz: 50
  //   _555: Hz: 5
  //   VCC: default 1
  //   nREQ: default 1
  //   nNMI: default 1
  //   nIRQ: default 1
  //   External Pinout
  //   CLK
  //   ~RST
  //   Buses & Constants
  //   Registers
  //   rom_1 loads sim_test.bin
endmodule
