// Digital circuit address_offset.dig as structural Verilog
module address_offset (
  input  [7:0] dbus,
  input  [15:0] addr_in,
  input  noffset_en,
  input  carry_en,
  input  naddr_xfer_assert,
  input  nassert_addr,
  input  clr,
  input  noffset_load,
  input  nclock,
  output [15:0] addr_out,
  output [15:0] xfer,
  output [7:0] q
);

  wire [7:0] multiplexer_1_out;
  wire [15:0] add_1_s, bitextender_1_out;

  // _74ls173 _74ls173_1: pin names not known; wires that end beside it: dbus[3:0], clr, nclock, noffset_load, noffset_load, 1'b0, 1'b0, 1'b1, 1'b0, q[3:0]
  // _74ls173 _74ls173_2: pin names not known; wires that end beside it: dbus[7:4], clr, nclock, noffset_load, noffset_load, 1'b0, 1'b0, 1'b1, 1'b0, q[7:4]
  Multiplexer #(.Bits(8)) multiplexer_1 (.sel(noffset_en), .in_0(q), .in_1({8{1'b0}}), .out(multiplexer_1_out));
  BitExtender bitextender_1 (.in(multiplexer_1_out), .out(bitextender_1_out));
  Add #(.Bits(16)) add_1 (.a(addr_in), .b(bitextender_1_out), .c_i(carry_en), .s(add_1_s));  // open: c_o
  _74ls245 _74ls245_1 (.DIR(1'b1), .nOE(naddr_xfer_assert), .A(add_1_s[7:0]), .B(xfer[7:0]), .VCC(1'b1), .GND(1'b0));
  _74ls245 _74ls245_2 (.DIR(1'b1), .nOE(naddr_xfer_assert), .A(add_1_s[15:8]), .B(xfer[15:8]), .VCC(1'b1), .GND(1'b0));
  _74ls245 _74ls245_3 (.DIR(1'b1), .nOE(nassert_addr), .A(add_1_s[7:0]), .B(addr_out[7:0]), .VCC(1'b1), .GND(1'b0));
  _74ls245 _74ls245_4 (.DIR(1'b1), .nOE(nassert_addr), .A(add_1_s[15:8]), .B(addr_out[15:8]), .VCC(1'b1), .GND(1'b0));

  // Other names for the same wires on the sheet: offset[7:0] = q; nclk = nclock; nload = noffset_load
endmodule
