// Digital circuit address_register.dig as structural Verilog
module address_register (
  input  [15:0] xfer,
  input  clr,
  input  nxfer_load,
  input  naddr_assert,
  input  nxfer_assert,
  input  inc,
  input  dec,
  input  clk,
  input  nhi_dbus_load,
  input  nlo_dbus_load,
  input  [7:0] dbus,
  output [15:0] addr,
  output [15:0] \reg 
);

  wire Bits_4_7_p2, Bits_4_7_p3, Bits_8_11_p2, Bits_8_11_p3, Bits_12_15_p2, Bits_12_15_p3, d0, d1, d2, d3,
       d4, d5, d6, d7, d8, d9, d10, d11, d12, d13, d14, d15, load_hi, load_lo, notconnected_1_out,
       notconnected_2_out, notconnected_3_out, notconnected_4_out;

  // NotConnected on notconnected_1_out
  // NotConnected on notconnected_2_out
  // NotConnected on notconnected_3_out
  // NotConnected on notconnected_4_out
  // _7408 load_control: pin names not known; wires that end beside it: nxfer_load, nhi_dbus_load, nxfer_load, nlo_dbus_load, notconnected_1_out, notconnected_2_out, notconnected_3_out, notconnected_4_out, 1'b1, 1'b0, load_hi, load_lo
  _74ls157 Nibble_b11_MUX (
    .S(nhi_dbus_load), .A(dbus[7:4]), .B(xfer[15:12]), .G(1'b0), .VCC(1'b1), .GND(1'b0),
    .Y({d15, d14, d13, d12}));
  // _74193 Bits_12_15: pin names not known; wires that end beside it: d12, Bits_12_15_p2, Bits_12_15_p3, d13, d14, d15, clr, load_hi, 1'b1, 1'b0, \reg [12], \reg [13], \reg [14], \reg [15]
  // _74574 _74574_1: pin names not known; wires that end beside it: nxfer_assert, clk, \reg [8], \reg [9], \reg [10], \reg [11], \reg [12], \reg [13], \reg [14], \reg [15], 1'b1, 1'b0, xfer[8], xfer[9], xfer[10], xfer[11], xfer[12], xfer[13], xfer[14], xfer[15]
  _74ls157 Nibble_b10_MUX (
    .S(nhi_dbus_load), .A(dbus[7:4]), .B(xfer[11:8]), .G(1'b0), .VCC(1'b1), .GND(1'b0), .Y({d11, d10, d9, d8}));
  // _74193 Bits_8_11: pin names not known; wires that end beside it: d8, Bits_8_11_p2, Bits_8_11_p3, d9, d10, d11, clr, load_hi, 1'b1, 1'b0, Bits_12_15_p2, Bits_12_15_p3, \reg [8], \reg [9], \reg [10], \reg [11]
  // _74574 _74574_2: pin names not known; wires that end beside it: nxfer_assert, clk, \reg [0], \reg [1], \reg [2], \reg [3], \reg [4], \reg [5], \reg [6], \reg [7], 1'b1, 1'b0, xfer[0], xfer[1], xfer[2], xfer[3], xfer[4], xfer[5], xfer[6], xfer[7]
  _74ls157 Nibble_b01_MUX (
    .S(nlo_dbus_load), .A(dbus[3:0]), .B(xfer[7:4]), .G(1'b0), .VCC(1'b1), .GND(1'b0), .Y({d7, d6, d5, d4}));
  // _74193 Bits_4_7: pin names not known; wires that end beside it: d4, Bits_4_7_p2, Bits_4_7_p3, d5, d6, d7, clr, load_lo, 1'b1, 1'b0, Bits_8_11_p2, Bits_8_11_p3, \reg [4], \reg [5], \reg [6], \reg [7]
  // _74574 _74574_3: pin names not known; wires that end beside it: naddr_assert, clk, \reg [8], \reg [9], \reg [10], \reg [11], \reg [12], \reg [13], \reg [14], \reg [15], 1'b1, 1'b0, addr[8], addr[9], addr[10], addr[11], addr[12], addr[13], addr[14], addr[15]
  _74ls157 Nibble_b00_MUX (
    .S(nlo_dbus_load), .A(dbus[3:0]), .B(xfer[3:0]), .G(1'b0), .VCC(1'b1), .GND(1'b0), .Y({d3, d2, d1, d0}));
  // _74193 Bits_0_3: pin names not known; wires that end beside it: d0, dec, inc, d1, d2, d3, clr, load_lo, 1'b1, 1'b0, Bits_4_7_p2, Bits_4_7_p3, \reg [0], \reg [1], \reg [2], \reg [3], clr
  // _74574 _74574_4: pin names not known; wires that end beside it: naddr_assert, clk, \reg [0], \reg [1], \reg [2], \reg [3], \reg [4], \reg [5], \reg [6], \reg [7], 1'b1, 1'b0, addr[0], addr[1], addr[2], addr[3], addr[4], addr[5], addr[6], addr[7]

  // Other names for the same wires on the sheet: addr_assert = naddr_assert; dbus_lo[3:0] = dbus[3:0];
  //   dbus_hi[3:0] = dbus[7:4]; hi_dbus_load = nhi_dbus_load; lo_dbus_load = nlo_dbus_load; q0 = \reg [0];
  //   q1 = \reg [1]; q2 = \reg [2]; q3 = \reg [3]; q4 = \reg [4]; q5 = \reg [5]; q6 = \reg [6]; q7 = \reg [7];
  //   q8 = \reg [8]; q9 = \reg [9]; q10 = \reg [10]; q11 = \reg [11]; q12 = \reg [12]; q13 = \reg [13];
  //   q14 = \reg [14]; q15 = \reg [15]; xfer_00[3:0] = xfer[3:0]; xfer_01[3:0] = xfer[7:4]; xfer_10[3:0] = xfer[11:8];
  //   xfer_11[3:0] = xfer[15:12]; xfer_assert = nxfer_assert; xfer_load = nxfer_load

  // Notes on the sheet:
  //   clr: default 1
  //   nxfer_load: default 1
  //   naddr_assert: default 1
  //   nxfer_assert: default 1
  //   inc: default 1
  //   dec: default 1
  //   nhi_dbus_load: default 1
  //   nlo_dbus_load: default 1
endmodule
