// Digital circuit alu.dig as structural Verilog
module alu (
  input  [3:0] alu_op,
  input  load_sr_dbus,
  input  assert_sr_dbus,
  input  clk,
  input  clr,
  input  [7:0] lhs,
  input  [7:0] rhs,
  input  assert_alu_dbus,
  input  set_nmi_inhib,
  input  clr_ubr,
  input  set_ubr,
  input  set_sup,
  output [7:0] flags,
  output [7:0] dbus,
  output [7:0] q
);

  wire _74ls260_1__1y, _74ls260_1__2y, C_fnew, c_shift, c_sum, I_fnew, N_fnew, Negative_Flag_Select_p8,
       Negative_Flag_Select_p9, Negative_Flag_Select_p10, Negative_Flag_Select_p11, Negative_Flag_Select_p12,
       notconnected_6_out, notconnected_7_out, notconnected_8_out, notconnected_9_out, notconnected_10_out,
       notconnected_11_out, notconnected_12_out, notconnected_13_out, notconnected_14_out,
       notconnected_15_out, Overflow_Flag_Select_p8, Overflow_Flag_Select_p9, Overflow_Flag_Select_p10,
       Overflow_Flag_Select_p11, Overflow_Flag_Select_p12, sel_cf_0, sel_cf_1, sel_cf_2, sel_if_0, sel_if_1,
       sel_nf_0, sel_nf_1, sel_vf_0, sel_vf_1, sel_zf_0, sel_zf_1, V, V_fnew, Z, Z_fnew;
  wire [1:0] sel_shift, sel_sum;
  wire [3:0] sel_logic;
  wire [7:0] A, B;

  alu_diode_matrix Diode_Matrix_Decoder (
    .ALU_OP(alu_op), .Sel_Cin_0(sel_sum[0]), .Sel_Cin_1(sel_sum[1]), .Sel_Shift_0(sel_shift[0]),
    .Sel_Shift_1(sel_shift[1]), .Sel_Logic_0(sel_logic[0]), .Sel_Logic_1(sel_logic[1]),
    .Sel_Logic_2(sel_logic[2]), .Sel_Logic_3(sel_logic[3]), .Sel_Cf_0(sel_cf_0), .Sel_Cf_1(sel_cf_1),
    .Sel_Cf_2(sel_cf_2), .Sel_Zf_0(sel_zf_0), .Sel_Zf_1(sel_zf_1), .Sel_Vf_0(sel_vf_0), .Sel_Vf_1(sel_vf_1),
    .Sel_Nf_0(sel_nf_0), .Sel_Nf_1(sel_nf_1), .Sel_If_0(sel_if_0), .Sel_If_1(sel_if_1));
  // _74151 Carry_Flag_Select: pin names not known; wires that end beside it: sel_cf_0, sel_cf_2, sel_cf_1, 1'b0, 1'b1, c_shift, c_sum, 1'b0, flags[4], flags[4], flags[4], flags[4], 1'b1, 1'b0, C_fnew
  // _74153 Negative_Flag_Select: pin names not known; wires that end beside it: sel_nf_0, sel_nf_1, 1'b0, 1'b1, q[7], 1'b0, flags[1], Negative_Flag_Select_p8, Negative_Flag_Select_p9, Negative_Flag_Select_p10, Negative_Flag_Select_p11, Negative_Flag_Select_p12, 1'b1, 1'b0, N_fnew
  // NotConnected on Negative_Flag_Select_p8
  // NotConnected on Negative_Flag_Select_p9
  // NotConnected on Negative_Flag_Select_p10
  // NotConnected on Negative_Flag_Select_p11
  // NotConnected on Negative_Flag_Select_p12
  // NotConnected on notconnected_6_out
  // NotConnected on notconnected_7_out
  // NotConnected on notconnected_8_out
  // NotConnected on notconnected_9_out
  // NotConnected on notconnected_10_out
  // NotConnected on notconnected_11_out
  // NotConnected on notconnected_12_out
  // NotConnected on notconnected_13_out
  // NotConnected on notconnected_14_out
  // NotConnected on notconnected_15_out
  // _74153 Zero_Flag_Select: pin names not known; wires that end beside it: sel_zf_0, sel_zf_1, 1'b0, 1'b1, Z, 1'b0, flags[3], notconnected_6_out, notconnected_7_out, notconnected_8_out, notconnected_9_out, notconnected_10_out, 1'b1, 1'b0, Z_fnew
  // _74153 Interrupt_Flag_Select: pin names not known; wires that end beside it: sel_if_0, sel_if_1, 1'b0, 1'b1, 1'b0, 1'b0, flags[0], notconnected_11_out, notconnected_12_out, notconnected_13_out, notconnected_14_out, notconnected_15_out, 1'b1, 1'b0, I_fnew
  // _74153 Overflow_Flag_Select: pin names not known; wires that end beside it: sel_vf_0, sel_vf_1, 1'b0, 1'b1, V, 1'b0, flags[2], Overflow_Flag_Select_p8, Overflow_Flag_Select_p9, Overflow_Flag_Select_p10, Overflow_Flag_Select_p11, Overflow_Flag_Select_p12, 1'b1, 1'b0, V_fnew
  // NotConnected on Overflow_Flag_Select_p8
  // NotConnected on Overflow_Flag_Select_p9
  // NotConnected on Overflow_Flag_Select_p10
  // NotConnected on Overflow_Flag_Select_p11
  // NotConnected on Overflow_Flag_Select_p12
  alu_arithmetic_unit alu_arithmetic_unit_1 (
    .left(A), .right(B), .sum_func_sel(sel_sum), .C_f(flags[4]), .C_fout(c_sum), .sum(q));
  alu_shift_unit alu_shift_unit_1 (.shift_func_sel(sel_shift), .lhs(lhs), .C_fin(flags[4]), .Q(A), .C_fout(c_shift));
  alu_status_register Status_Register (
    .DBUS(dbus), .ALU({C_fnew, Z_fnew, V_fnew, N_fnew, I_fnew}), .CLR(clr), .CLK(clk),
    .ASSERT(assert_sr_dbus), .LOAD_DBUS(load_sr_dbus), .nSet_nSUP(set_sup), .nSet_nUBR(set_ubr),
    .nClear_nUBR(clr_ubr), .nSet_nNMI_nInhibit(set_nmi_inhib), .flags(flags));
  alu_logic_unit alu_logic_unit_1 (.logic_func_sel(sel_logic), .rhs(rhs), .lhs(lhs), .Q(B));
  _74ls245 _74ls245_1 (.DIR(1'b1), .nOE(assert_alu_dbus), .A(q), .B(dbus), .VCC(1'b1), .GND(1'b0));
  _74ls260 _74ls260_1 (
    ._1A(q[0]), ._2A(q[1]), ._3A(q[2]), ._4A(q[3]), ._5A(1'b0), ._1B(q[4]), ._2B(q[5]), ._3B(q[6]),
    ._4B(q[7]), ._5B(1'b0), .VCC(1'b1), .GND(1'b0), ._1Y(_74ls260_1__1y), ._2Y(_74ls260_1__2y));
  // _74151 _74151_1: pin names not known; wires that end beside it: 1'b0, 1'b1, rhs[7], q[7], lhs[7], 1'b0, 1'b0, 1'b0, 1'b0, 1'b1, 1'b1, 1'b0, 1'b0, 1'b0, 1'b1, 1'b0, V
  // _7408 _7408_1: pin names not known; wires that end beside it: _74ls260_1__1y, _74ls260_1__2y, 1'b0, 1'b0, 1'b0, 1'b0, 1'b0, 1'b0, 1'b1, 1'b0, Z, 1'b0, 1'b0, 1'b0

  // Other names for the same wires on the sheet: I_f = flags[0]; N_f = flags[1]; V_f = flags[2]; Z_f = flags[3];
  //   C_f = flags[4]; U_nS_f = flags[5]; UBR_f = flags[6]; NMI_I_f = flags[7]; assert_alu = assert_alu_dbus;
  //   assert_sr = assert_sr_dbus; load = load_sr_dbus; s0 = q[0]; s1 = q[1]; s2 = q[2]; s3 = q[3]; s4 = q[4];
  //   s5 = q[5]; s6 = q[6]; N = q[7]; s7 = q[7]

  // Notes on the sheet:
  //   load_sr_dbus: default 1
  //   assert_sr_dbus: default 1
  //   assert_alu_dbus: default 1
  //   Determine what ALU Contributes to SR
  //   Status Register (Dual Source Register)
  //   ALU Core with DBUS Output
  //   Zero Flag Determination
  //   Sign (Negative) Flag Determination
  //   Overflow Flag Determination
endmodule

/* Test case:
alu-op     dbus       load-sr-dbus assert-sr-dbus assert-alu-dbus clk clr lhs rhs flags    q
0          Z          1            1              1               0   0   X   X   0b00000  0
0          0          1            1              0               0   0   X   X   0b00000  0
1          Z          1            1              1               C   0   1   2   X        3
1          Z          1            1              1               C   0   0   0   0b01000  0
14         Z          1            1              1               C   0   X   X   0b01000  0
1          Z          1            1              1               C   0   255 1   0b11000  0
*/
