// Digital circuit alu_arithmetic_unit.dig as structural Verilog
module alu_arithmetic_unit (
  input  [7:0] left,
  input  [7:0] right,
  input  [1:0] sum_func_sel,
  input  C_f,
  output C_fout,
  output [7:0] sum
);

  wire _74ls283_1_c_out, _74151_1_p17;

  // _74151 _74151_1: pin names not known; wires that end beside it: 1'b0, 1'b1, sum_func_sel[0], C_f, sum_func_sel[1], 1'b0, 1'b0, 1'b0, 1'b0, 1'b1, 1'b0, 1'b1, 1'b1, 1'b1, 1'b1, 1'b0, _74151_1_p17
  _74ls283 _74ls283_1 (
    .A(left[3:0]), .B(right[3:0]), .C_in(_74151_1_p17), .VCC(1'b1), .GND(1'b0), .S(sum[3:0]),
    .C_out(_74ls283_1_c_out));
  _74ls283 _74ls283_2 (
    .A(left[7:4]), .B(right[7:4]), .C_in(_74ls283_1_c_out), .VCC(1'b1), .GND(1'b0), .S(sum[7:4]),
    .C_out(C_fout));

  // Other names for the same wires on the sheet: left_lo[3:0] = left[3:0]; left_hi[3:0] = left[7:4];
  //   right_lo[3:0] = right[3:0]; right_hi[3:0] = right[7:4]; s_hi[3:0] = sum[7:4]; s_lo[3:0] = sum[3:0]
endmodule
