// Digital circuit alu_diode_matrix.dig as structural Verilog
module alu_diode_matrix (
  input  [3:0] ALU_OP,
  output Sel_Cin_0,
  output Sel_Cin_1,
  output Sel_Shift_0,
  output Sel_Shift_1,
  output Sel_Logic_0,
  output Sel_Logic_1,
  output Sel_Logic_2,
  output Sel_Logic_3,
  output Sel_Cf_0,
  output Sel_Cf_1,
  output Sel_Cf_2,
  output Sel_Zf_0,
  output Sel_Zf_1,
  output Sel_Vf_0,
  output Sel_Vf_1,
  output Sel_Nf_0,
  output Sel_Nf_1,
  output Sel_If_0,
  output Sel_If_1
);

  wire _74138_1_p2, _74138_1_p4, _74138_1_p6, _74138_1_p8, _74138_1_p10, _74138_1_p12, _74138_1_p14,
       _74138_1_p16, _74138_1_p18, _74138_1_p20, _74138_1_p22, _74138_2_p2, _74138_2_p4, _74138_2_p6,
       _74138_2_p8, _74138_2_p10;

  PullUp pullup_1 (.out(Sel_Cin_0));
  PullUp pullup_2 (.out(Sel_Cin_1));
  PullUp pullup_3 (.out(Sel_Shift_0));
  PullUp pullup_4 (.out(Sel_Shift_1));
  PullUp pullup_5 (.out(Sel_Logic_0));
  PullUp pullup_6 (.out(Sel_Logic_1));
  PullUp pullup_7 (.out(Sel_Logic_2));
  PullUp pullup_8 (.out(Sel_Logic_3));
  PullUp pullup_9 (.out(Sel_Cf_0));
  PullUp pullup_10 (.out(Sel_Cf_1));
  PullUp pullup_11 (.out(Sel_Cf_2));
  PullUp pullup_12 (.out(Sel_Zf_0));
  PullUp pullup_13 (.out(Sel_Zf_1));
  DiodeBackward diodebackward_1 (.in(_74138_1_p2), .out(Sel_Vf_0));
  PullUp pullup_14 (.out(Sel_Vf_0));
  PullUp pullup_15 (.out(Sel_Vf_1));
  PullUp pullup_16 (.out(Sel_Nf_0));
  PullUp pullup_17 (.out(Sel_Nf_1));
  PullUp pullup_18 (.out(Sel_If_0));
  PullUp pullup_19 (.out(Sel_If_1));
  DiodeBackward diodebackward_2 (.in(_74138_1_p6), .out(Sel_Cf_0));
  DiodeBackward diodebackward_3 (.in(_74138_1_p6), .out(Sel_Cf_1));
  DiodeBackward diodebackward_4 (.in(_74138_1_p6), .out(Sel_Cf_2));
  DiodeBackward diodebackward_5 (.in(_74138_1_p4), .out(Sel_Cf_2));
  DiodeBackward diodebackward_6 (.in(_74138_1_p10), .out(Sel_If_0));
  DiodeBackward diodebackward_7 (.in(_74138_1_p10), .out(Sel_If_1));
  DiodeBackward diodebackward_8 (.in(_74138_1_p8), .out(Sel_If_1));
  DiodeBackward diodebackward_9 (.in(_74138_1_p14), .out(Sel_Cin_0));
  DiodeBackward diodebackward_10 (.in(_74138_1_p12), .out(Sel_Cin_0));
  DiodeBackward diodebackward_11 (.in(_74138_1_p14), .out(Sel_Cin_1));
  DiodeBackward diodebackward_12 (.in(_74138_1_p12), .out(Sel_Cin_1));
  DiodeBackward diodebackward_13 (.in(_74138_1_p12), .out(Sel_Shift_0));
  DiodeBackward diodebackward_14 (.in(_74138_1_p14), .out(Sel_Shift_1));
  DiodeBackward diodebackward_15 (.in(_74138_1_p14), .out(Sel_Logic_0));
  DiodeBackward diodebackward_16 (.in(_74138_1_p12), .out(Sel_Logic_0));
  DiodeBackward diodebackward_17 (.in(_74138_1_p14), .out(Sel_Logic_1));
  DiodeBackward diodebackward_18 (.in(_74138_1_p12), .out(Sel_Logic_1));
  DiodeBackward diodebackward_19 (.in(_74138_1_p14), .out(Sel_Logic_2));
  DiodeBackward diodebackward_20 (.in(_74138_1_p12), .out(Sel_Logic_2));
  DiodeBackward diodebackward_21 (.in(_74138_1_p14), .out(Sel_Logic_3));
  DiodeBackward diodebackward_22 (.in(_74138_1_p12), .out(Sel_Logic_3));
  DiodeBackward diodebackward_23 (.in(_74138_1_p14), .out(Sel_Cf_1));
  DiodeBackward diodebackward_24 (.in(_74138_1_p12), .out(Sel_Cf_1));
  DiodeBackward diodebackward_25 (.in(_74138_1_p14), .out(Sel_Cf_2));
  DiodeBackward diodebackward_26 (.in(_74138_1_p12), .out(Sel_Cf_2));
  DiodeBackward diodebackward_27 (.in(_74138_1_p14), .out(Sel_Zf_1));
  DiodeBackward diodebackward_28 (.in(_74138_1_p12), .out(Sel_Zf_1));
  DiodeBackward diodebackward_29 (.in(_74138_1_p14), .out(Sel_Nf_1));
  DiodeBackward diodebackward_30 (.in(_74138_1_p12), .out(Sel_Nf_1));
  // _74138 _74138_1: pin names not known; wires that end beside it: 1'b0, _74138_1_p2, 1'b1, _74138_1_p4, 1'b0, _74138_1_p6, 1'b0, _74138_1_p8, ALU_OP[3], _74138_1_p10, ALU_OP[1], _74138_1_p12, ALU_OP[2], _74138_1_p14, ALU_OP[0], _74138_1_p16, 1'b0, _74138_1_p18, 1'b1, _74138_1_p20, 1'b0, _74138_1_p22
  DiodeBackward diodebackward_31 (.in(_74138_1_p18), .out(Sel_Cin_0));
  DiodeBackward diodebackward_32 (.in(_74138_1_p16), .out(Sel_Cin_0));
  DiodeBackward diodebackward_33 (.in(_74138_1_p18), .out(Sel_Cin_1));
  DiodeBackward diodebackward_34 (.in(_74138_1_p16), .out(Sel_Cin_1));
  DiodeBackward diodebackward_35 (.in(_74138_1_p18), .out(Sel_Logic_0));
  DiodeBackward diodebackward_36 (.in(_74138_1_p16), .out(Sel_Logic_2));
  DiodeBackward diodebackward_37 (.in(_74138_1_p18), .out(Sel_Logic_3));
  DiodeBackward diodebackward_38 (.in(_74138_1_p16), .out(Sel_Logic_3));
  DiodeBackward diodebackward_39 (.in(_74138_1_p18), .out(Sel_Zf_1));
  DiodeBackward diodebackward_40 (.in(_74138_1_p16), .out(Sel_Zf_1));
  DiodeBackward diodebackward_41 (.in(_74138_1_p18), .out(Sel_Nf_1));
  DiodeBackward diodebackward_42 (.in(_74138_1_p16), .out(Sel_Nf_1));
  DiodeBackward diodebackward_43 (.in(_74138_1_p22), .out(Sel_Cin_0));
  DiodeBackward diodebackward_44 (.in(_74138_1_p20), .out(Sel_Cin_0));
  DiodeBackward diodebackward_45 (.in(_74138_1_p22), .out(Sel_Cin_1));
  DiodeBackward diodebackward_46 (.in(_74138_1_p20), .out(Sel_Cin_1));
  DiodeBackward diodebackward_47 (.in(_74138_1_p22), .out(Sel_Logic_0));
  DiodeBackward diodebackward_48 (.in(_74138_1_p20), .out(Sel_Logic_0));
  DiodeBackward diodebackward_49 (.in(_74138_1_p22), .out(Sel_Logic_1));
  DiodeBackward diodebackward_50 (.in(_74138_1_p22), .out(Sel_Logic_2));
  DiodeBackward diodebackward_51 (.in(_74138_1_p22), .out(Sel_Zf_1));
  DiodeBackward diodebackward_52 (.in(_74138_1_p20), .out(Sel_Zf_1));
  DiodeBackward diodebackward_53 (.in(_74138_1_p22), .out(Sel_Nf_1));
  DiodeBackward diodebackward_54 (.in(_74138_1_p20), .out(Sel_Nf_1));
  // _74138 _74138_2: pin names not known; wires that end beside it: ALU_OP[3], _74138_2_p2, 1'b1, _74138_2_p4, ALU_OP[1], _74138_2_p6, ALU_OP[2], _74138_2_p8, ALU_OP[0], _74138_2_p10
  DiodeBackward diodebackward_55 (.in(_74138_2_p2), .out(Sel_Cin_0));
  DiodeBackward diodebackward_56 (.in(_74138_2_p2), .out(Sel_Cin_1));
  DiodeBackward diodebackward_57 (.in(_74138_2_p2), .out(Sel_Shift_0));
  DiodeBackward diodebackward_58 (.in(_74138_2_p2), .out(Sel_Shift_1));
  DiodeBackward diodebackward_59 (.in(_74138_2_p4), .out(Sel_Logic_0));
  DiodeBackward diodebackward_60 (.in(_74138_2_p4), .out(Sel_Logic_1));
  DiodeBackward diodebackward_61 (.in(_74138_2_p4), .out(Sel_Cf_0));
  DiodeBackward diodebackward_62 (.in(_74138_2_p2), .out(Sel_Cf_0));
  DiodeBackward diodebackward_63 (.in(_74138_2_p4), .out(Sel_Cf_2));
  DiodeBackward diodebackward_64 (.in(_74138_2_p2), .out(Sel_Cf_2));
  DiodeBackward diodebackward_65 (.in(_74138_2_p4), .out(Sel_Zf_1));
  DiodeBackward diodebackward_66 (.in(_74138_2_p2), .out(Sel_Zf_1));
  DiodeBackward diodebackward_67 (.in(_74138_2_p4), .out(Sel_Nf_1));
  DiodeBackward diodebackward_68 (.in(_74138_2_p2), .out(Sel_Nf_1));
  DiodeBackward diodebackward_69 (.in(_74138_2_p8), .out(Sel_Cin_1));
  DiodeBackward diodebackward_70 (.in(_74138_2_p6), .out(Sel_Cin_1));
  DiodeBackward diodebackward_71 (.in(_74138_2_p8), .out(Sel_Shift_0));
  DiodeBackward diodebackward_72 (.in(_74138_2_p6), .out(Sel_Shift_0));
  DiodeBackward diodebackward_73 (.in(_74138_2_p8), .out(Sel_Shift_1));
  DiodeBackward diodebackward_74 (.in(_74138_2_p6), .out(Sel_Shift_1));
  DiodeBackward diodebackward_75 (.in(_74138_2_p8), .out(Sel_Logic_0));
  DiodeBackward diodebackward_76 (.in(_74138_2_p8), .out(Sel_Logic_1));
  DiodeBackward diodebackward_77 (.in(_74138_2_p6), .out(Sel_Logic_2));
  DiodeBackward diodebackward_78 (.in(_74138_2_p6), .out(Sel_Logic_3));
  DiodeBackward diodebackward_79 (.in(_74138_2_p8), .out(Sel_Cf_0));
  DiodeBackward diodebackward_80 (.in(_74138_2_p6), .out(Sel_Cf_0));
  DiodeBackward diodebackward_81 (.in(_74138_2_p8), .out(Sel_Cf_2));
  DiodeBackward diodebackward_82 (.in(_74138_2_p6), .out(Sel_Cf_2));
  DiodeBackward diodebackward_83 (.in(_74138_2_p8), .out(Sel_Zf_1));
  DiodeBackward diodebackward_84 (.in(_74138_2_p6), .out(Sel_Zf_1));
  DiodeBackward diodebackward_85 (.in(_74138_2_p8), .out(Sel_Vf_1));
  DiodeBackward diodebackward_86 (.in(_74138_2_p6), .out(Sel_Vf_1));
  DiodeBackward diodebackward_87 (.in(_74138_2_p8), .out(Sel_Nf_1));
  DiodeBackward diodebackward_88 (.in(_74138_2_p6), .out(Sel_Nf_1));
  DiodeBackward diodebackward_89 (.in(_74138_2_p10), .out(Sel_Cin_0));
  DiodeBackward diodebackward_90 (.in(_74138_2_p10), .out(Sel_Cin_1));
  DiodeBackward diodebackward_91 (.in(_74138_2_p10), .out(Sel_Logic_0));
  DiodeBackward diodebackward_92 (.in(_74138_2_p10), .out(Sel_Logic_1));
  DiodeBackward diodebackward_93 (.in(_74138_2_p10), .out(Sel_Logic_2));
  DiodeBackward diodebackward_94 (.in(_74138_2_p10), .out(Sel_Logic_3));

  // Notes on the sheet:
  //   CLV
  //   SEC
  //   CLC
  //   SEI
  //   CLI
  //   LRC
  //   ASR
  //   XOR
  //   NOT
  //   AND
  //   OR
  //   INC
  //   DEC
  //   ADC
  //   SBB
  //   NOP
endmodule

/* Test case:
ALU-OP Sel-Shift-1 Sel-Shift-0 Sel-Logic-3 Sel-Logic-2 Sel-Logic-1 Sel-Logic-0 Sel-Cin-1 Sel-Cin-0 Sel-Cf-2 Sel-Cf-1 Sel-Cf-0 Sel-Zf-1 Sel-Zf-0 Sel-Vf-1 Sel-Vf-0 Sel-Nf-1 Sel-Nf-0 Sel-If-1 Sel-If-0
# NOP
0 1 1 0 0 0 0 0 0 1 1 1 1 1 1 1 1 1 1 1
# ADC
1 0 0 1 1 0 0 0 1 0 1 0 0 1 0 1 0 1 1 1
# SBC
2 0 0 0 0 1 1 0 1 0 1 0 0 1 0 1 0 1 1 1
# INC
3 1 1 1 1 0 0 1 1 0 1 0 0 1 1 1 0 1 1 1
# DEC
4 0 0 1 1 1 1 0 0 0 1 0 0 1 1 1 0 1 1 1
# AND
5 1 1 1 0 0 0 0 0 1 1 1 0 1 1 1 0 1 1 1
# OR
6 1 1 1 1 1 0 0 0 1 1 1 0 1 1 1 0 1 1 1
# XOR
7 1 1 0 1 1 0 0 0 1 1 1 0 1 1 1 0 1 1 1
# NOT
8 1 1 0 0 1 1 0 0 1 1 1 0 1 1 1 0 1 1 1
# SRC
9 0 1 0 0 0 0 0 0 0 0 1 0 1 1 1 0 1 1 1
# ASR
10 1 0 0 0 0 0 0 0 0 0 1 0 1 1 1 0 1 1 1
# SEI
11 1 1 1 1 1 1 1 1 1 1 1 1 1 1 1 1 1 0 0
# CLI
12 1 1 1 1 1 1 1 1 1 1 1 1 1 1 1 1 1 0 1
# SEC
13 1 1 1 1 1 1 1 1 0 0 0 1 1 1 1 1 1 1 1
# CLC
14 1 1 1 1 1 1 1 1 0 1 1 1 1 1 1 1 1 1 1
# CLV
15 1 1 1 1 1 1 1 1 1 1 1 1 1 1 0 1 1 1 1
*/
