// Digital circuit alu_status_register.dig as structural Verilog
module alu_status_register (
  input  [7:0] DBUS,
  input  [7:0] ALU,
  input  CLR,
  input  CLK,
  input  ASSERT,
  input  LOAD_DBUS,
  output [7:0] flags
);

  wire [3:0] Source_Select_Hi_y, Source_Select_Lo_y;

  _74ls157 Source_Select_Hi (
    .S(LOAD_DBUS), .A(DBUS[7:4]), .B(ALU[7:4]), .G(1'b0), .VCC(1'b1), .GND(1'b0), .Y(Source_Select_Hi_y));
  _74ls157 Source_Select_Lo (
    .S(LOAD_DBUS), .A(DBUS[3:0]), .B(ALU[3:0]), .G(1'b0), .VCC(1'b1), .GND(1'b0), .Y(Source_Select_Lo_y));
  // _74ls173 Status_Hi: pin names not known; wires that end beside it: Source_Select_Hi_y, 1'b1, 1'b0, CLR, CLK, 1'b0, 1'b0, 1'b0, 1'b0, flags[7:4]
  // _74ls173 Status_Lo: pin names not known; wires that end beside it: Source_Select_Lo_y, 1'b1, 1'b0, CLR, CLK, 1'b0, 1'b0, 1'b0, 1'b0, flags[3:0]
  _74ls245 to_DBUS (.DIR(1'b1), .nOE(ASSERT), .A(flags), .B(DBUS), .VCC(1'b1), .GND(1'b0));

  // Other names for the same wires on the sheet: alu_lo[3:0] = ALU[3:0]; alu_hi[3:0] = ALU[7:4];
  //   dbus_lo[3:0] = DBUS[3:0]; dbus_hi[3:0] = DBUS[7:4]; load = LOAD_DBUS; q[7:0] = flags; q_hi[3:0] = flags[7:4];
  //   q_lo[3:0] = flags[3:0]

  // Notes on the sheet:
  //   ASSERT: default 1
endmodule
