// Digital circuit bus_controller.dig as structural Verilog
module bus_controller (
  input  [3:0] dbus_assert,
  input  [3:0] dbus_load,
  input  [4:0] xfer_assert,
  input  [2:0] xfer_load,
  input  [2:0] addr_assert,
  input  clk,
  input  [2:0] count,
  input  dec_sp,
  input  nclk,
  output ALU_dbus_assert,
  output A_dbus_assert,
  output B_dbus_assert,
  output C_dbus_assert,
  output D_dbus_assert,
  output SR_dbus_assert,
  output DP_dbus_assert,
  output T1_dbus_assert,
  output T2_dbus_assert,
  output MEM_dbus_load,
  output A_dbus_load,
  output B_dbus_load,
  output C_dbus_load,
  output D_dbus_load,
  output SR_dbus_load,
  output DP_dbus_load,
  output T1_dbus_load,
  output T2_dbus_load,
  output A_lhs_assert,
  output B_lhs_assert,
  output C_lhs_assert,
  output D_lhs_assert,
  output A_rhs_assert,
  output B_rhs_assert,
  output C_rhs_assert,
  output D_rhs_assert,
  output PC_xfer_assert,
  output SP_xfer_assert,
  output X_xfer_assert,
  output Y_xfer_assert,
  output ISR_xfer_assert,
  output RST_xfer_assert,
  output PC_xfer_load,
  output SP_xfer_load,
  output X_xfer_load,
  output Y_xfer_load,
  output E_xfer_load,
  output PC_addr_assert,
  output SP_addr_assert,
  output X_addr_assert,
  output Y_addr_assert,
  output E_addr_assert,
  output DP_addr_assert,
  output MEM_dbus_assert,
  output IR_dbus_load,
  output T1_rhs_assert,
  output PC_inc,
  output SP_inc,
  output X_inc,
  output Y_inc,
  output SP_dec,
  output X_dec,
  output Y_dec,
  output DPI_dbus_assert,
  output SPI_xfer_assert,
  output T_addr_assert,
  output ACK_addr_assert,
  output T_xfer_assert,
  output E_xfer_assert,
  output T_inc,
  output T2_lhs_assert,
  output zero_dbus_assert
);

  wire _7400_1_p3, _7400_1_p4, _7400_1_p5, _7400_1_p6, _7400_1_p7, _7400_1_p8, _7421_1_p11, _7421_1_p12,
       _7421_3_p11, _7421_3_p12, _74139_1_p9, _74139_1_p10, _74139_1_p11, _74139_1_p12, ndbus_a1, ndbus_a13,
       ndbus_a14, ndbus_a15, ndbus_l11, ndbus_l12, ndbus_l13, ndbus_l14, ndbus_l15, notconnected_1_out,
       notconnected_2_out, notconnected_3_out, notconnected_4_out, nxfer_a9, nxfer_a10, nxfer_a11, nxfer_a12,
       nxfer_a13, nxfer_a14, nxfer_a15, nxfer_a16, nxfer_a17, nxfer_a18, nxfer_a19, nxfer_a20, nxfer_a21,
       nxfer_a22, nxfer_a23, nxfer_a24, nxfer_a25, nxfer_a26, nxfer_a27, nxfer_a28, nxfer_a29, nxfer_a30,
       nxfer_a31, nxfer_l5, nxfer_l7, select_lhs_assert_p12, select_rhs_assert_p11;

  // _74138 DBUS_assert: pin names not known; wires that end beside it: dbus_assert[0], dbus_assert[2], dbus_assert[1], 1'b1, 1'b0, dbus_assert[3], 1'b1, 1'b0, zero_dbus_assert, ndbus_a1, A_dbus_assert, B_dbus_assert, C_dbus_assert, D_dbus_assert, DP_dbus_assert, SR_dbus_assert
  // _74138 _74138_1: pin names not known; wires that end beside it: dbus_assert[0], dbus_assert[2], dbus_assert[1], dbus_assert[3], 1'b0, 1'b0, 1'b1, 1'b0, T1_dbus_assert, T2_dbus_assert, MEM_dbus_assert, DPI_dbus_assert, ALU_dbus_assert, ndbus_a13, ndbus_a14, ndbus_a15
  // _74138 DBUS_load: pin names not known; wires that end beside it: dbus_assert[0], dbus_assert[2], dbus_assert[1], 1'b1, nclk, dbus_load[3], 1'b1, 1'b0, IR_dbus_load, A_dbus_load, B_dbus_load, C_dbus_load, D_dbus_load, DP_dbus_load, SR_dbus_load
  // _74138 _74138_2: pin names not known; wires that end beside it: dbus_load[0], dbus_load[2], dbus_load[1], dbus_load[3], nclk, 1'b0, 1'b1, 1'b0, T1_dbus_load, T2_dbus_load, ndbus_l11, ndbus_l12, ndbus_l13, ndbus_l14, ndbus_l15
  // _74138 DBUS_load__not_nclk_gated: pin names not known; wires that end beside it: dbus_load[0], dbus_load[2], dbus_load[1], dbus_load[3], 1'b0, 1'b0, 1'b1, 1'b0, MEM_dbus_load
  // _74139 _74139_1: pin names not known; wires that end beside it: xfer_assert[3], xfer_assert[4], 1'b0, 1'b1, 1'b1, 1'b1, 1'b1, 1'b0, _74139_1_p9, _74139_1_p10, _74139_1_p11, _74139_1_p12
  // _74138 XFER_assert: pin names not known; wires that end beside it: xfer_assert[0], xfer_assert[2], xfer_assert[1], 1'b1, 1'b0, _74139_1_p9, 1'b1, 1'b0, RST_xfer_assert, SP_xfer_assert, PC_xfer_assert, X_xfer_assert, Y_xfer_assert, T_xfer_assert, E_xfer_assert, ISR_xfer_assert
  // _74138 _74138_3: pin names not known; wires that end beside it: xfer_assert[0], xfer_assert[2], xfer_assert[1], 1'b1, 1'b0, _74139_1_p10, 1'b1, 1'b0, SPI_xfer_assert, nxfer_a9, nxfer_a10, nxfer_a11, nxfer_a12, nxfer_a13, nxfer_a14, nxfer_a15
  // _74138 _74138_4: pin names not known; wires that end beside it: xfer_assert[0], xfer_assert[2], xfer_assert[1], 1'b1, 1'b0, _74139_1_p11, 1'b1, 1'b0, nxfer_a16, nxfer_a17, nxfer_a18, nxfer_a19, nxfer_a20, nxfer_a21, nxfer_a22, nxfer_a23
  // _74138 _74138_5: pin names not known; wires that end beside it: xfer_assert[0], xfer_assert[2], xfer_assert[1], 1'b1, 1'b0, _74139_1_p12, 1'b1, 1'b0, nxfer_a24, nxfer_a25, nxfer_a26, nxfer_a27, nxfer_a28, nxfer_a29, nxfer_a30, nxfer_a31
  // _74138 XFER_load: pin names not known; wires that end beside it: xfer_load[0], xfer_load[2], xfer_load[1], 1'b1, nclk, 1'b0, 1'b1, 1'b0, SP_xfer_load, PC_xfer_load, X_xfer_load, Y_xfer_load, nxfer_l5, E_xfer_load, nxfer_l7
  // _74138 ADDR_assert: pin names not known; wires that end beside it: addr_assert[0], addr_assert[2], addr_assert[1], 1'b1, 1'b0, 1'b0, 1'b1, 1'b0, ACK_addr_assert, PC_addr_assert, SP_addr_assert, X_addr_assert, Y_addr_assert, E_addr_assert, DP_addr_assert, T_addr_assert
  // _74138 Counter_Inc_Dec: pin names not known; wires that end beside it: count[0], count[2], count[1], 1'b1, 1'b0, nclk, 1'b1, 1'b0, SP_inc, PC_inc, X_inc, Y_inc, T_inc, X_dec, Y_dec
  // _7421 select_lhs_assert: pin names not known; wires that end beside it: nxfer_a10, nxfer_a12, nxfer_a14, nxfer_a16, nxfer_a11, nxfer_a15, nxfer_a13, nxfer_a17, 1'b1, 1'b0, A_lhs_assert, select_lhs_assert_p12
  // _7421 _7421_1: pin names not known; wires that end beside it: nxfer_a19, nxfer_a21, nxfer_a24, nxfer_a26, nxfer_a20, nxfer_a25, nxfer_a22, nxfer_a27, 1'b1, 1'b0, _7421_1_p11, _7421_1_p12
  // _7421 _7421_2: pin names not known; wires that end beside it: nxfer_a29, nxfer_a31, nxfer_a13, nxfer_a23, nxfer_a30, nxfer_a18, nxfer_a9, nxfer_a28, 1'b1, 1'b0, T2_lhs_assert, T1_rhs_assert
  // _7421 select_rhs_assert: pin names not known; wires that end beside it: nxfer_a10, nxfer_a19, nxfer_a15, nxfer_a25, nxfer_a14, nxfer_a20, nxfer_a24, nxfer_a30, 1'b1, 1'b0, select_rhs_assert_p11, B_rhs_assert
  // _7421 _7421_3: pin names not known; wires that end beside it: nxfer_a11, nxfer_a21, nxfer_a12, nxfer_a22, nxfer_a16, nxfer_a17, nxfer_a26, nxfer_a27, 1'b1, 1'b0, _7421_3_p11, _7421_3_p12
  // NotConnected on notconnected_1_out
  // NotConnected on notconnected_2_out
  // NotConnected on notconnected_3_out
  // NotConnected on notconnected_4_out
  // _7408 _7408_1: pin names not known; wires that end beside it: select_lhs_assert_p12, nxfer_a18, _7421_1_p11, nxfer_a23, _7421_1_p12, nxfer_a28, notconnected_1_out, notconnected_2_out, 1'b1, 1'b0, B_lhs_assert, C_lhs_assert, D_lhs_assert
  // _7408 _7408_2: pin names not known; wires that end beside it: select_rhs_assert_p11, nxfer_a29, _7421_3_p11, nxfer_a31, _7421_3_p12, nxfer_a9, notconnected_3_out, notconnected_4_out, 1'b1, 1'b0, A_rhs_assert, C_rhs_assert, D_rhs_assert
  // _7400 _7400_1: pin names not known; wires that end beside it: clk, dec_sp, _7400_1_p3, _7400_1_p4, _7400_1_p5, _7400_1_p6, _7400_1_p7, _7400_1_p8, 1'b1, 1'b0, SP_dec
  // NotConnected on _7400_1_p3
  // NotConnected on _7400_1_p4
  // NotConnected on _7400_1_p5
  // NotConnected on _7400_1_p6
  // NotConnected on _7400_1_p7
  // NotConnected on _7400_1_p8

  // Other names for the same wires on the sheet: aa0 = addr_assert[0]; aa1 = addr_assert[1]; aa2 = addr_assert[2];
  //   ci0 = count[0]; ci1 = count[1]; ci2 = count[2]; da0 = dbus_assert[0]; da1 = dbus_assert[1];
  //   da2 = dbus_assert[2]; da3 = dbus_assert[3]; dl0 = dbus_load[0]; dl1 = dbus_load[1]; dl2 = dbus_load[2];
  //   dl3 = dbus_load[3]; naddr_a0 = ACK_addr_assert; naddr_a1 = PC_addr_assert; naddr_a2 = SP_addr_assert;
  //   naddr_a3 = X_addr_assert; naddr_a4 = Y_addr_assert; naddr_a5 = E_addr_assert; naddr_a6 = DP_addr_assert;
  //   naddr_a7 = T_addr_assert; ncount_1 = SP_inc; ncount_2 = PC_inc; ncount_3 = X_inc; ncount_4 = Y_inc;
  //   ncount_5 = T_inc; ncount_6 = X_dec; ncount_7 = Y_dec; ndbus_a0 = zero_dbus_assert; ndbus_a2 = A_dbus_assert;
  //   ndbus_a3 = B_dbus_assert; ndbus_a4 = C_dbus_assert; ndbus_a5 = D_dbus_assert; ndbus_a6 = DP_dbus_assert;
  //   ndbus_a7 = SR_dbus_assert; ndbus_a8 = T1_dbus_assert; ndbus_a9 = T2_dbus_assert; ndbus_a10 = MEM_dbus_assert;
  //   ndbus_a11 = DPI_dbus_assert; ndbus_a12 = ALU_dbus_assert; ndbus_l1 = IR_dbus_load; ndbus_l2 = A_dbus_load;
  //   ndbus_l3 = B_dbus_load; ndbus_l4 = C_dbus_load; ndbus_l5 = D_dbus_load; ndbus_l6 = DP_dbus_load;
  //   ndbus_l7 = SR_dbus_load; ndbus_l8 = T1_dbus_load; ndbus_l9 = T2_dbus_load; ndbus_l10 = MEM_dbus_load;
  //   nxfer_a0 = RST_xfer_assert; nxfer_a1 = SP_xfer_assert; nxfer_a2 = PC_xfer_assert; nxfer_a3 = X_xfer_assert;
  //   nxfer_a4 = Y_xfer_assert; nxfer_a5 = T_xfer_assert; nxfer_a6 = E_xfer_assert; nxfer_a7 = ISR_xfer_assert;
  //   nxfer_a8 = SPI_xfer_assert; nxfer_l1 = SP_xfer_load; nxfer_l2 = PC_xfer_load; nxfer_l3 = X_xfer_load;
  //   nxfer_l4 = Y_xfer_load; nxfer_l6 = E_xfer_load; xa0 = xfer_assert[0]; xa1 = xfer_assert[1];
  //   xa2 = xfer_assert[2]; xa3 = xfer_assert[3]; xa4 = xfer_assert[4]; xl0 = xfer_load[0]; xl1 = xfer_load[1];
  //   xl2 = xfer_load[2]
endmodule
