// Digital circuit constant_generator_16bit.dig as structural Verilog
module constant_generator_16bit (
  input  [15:0] ISRv_Hi,
  input  nASSERT_ISRvHi,
  output [15:0] xfer
);

  _74ls245 ISRv_Hi_to_XFER (.DIR(1'b1), .nOE(nASSERT_ISRvHi), .A(ISRv_Hi[7:0]), .B(xfer[7:0]), .VCC(1'b1), .GND(1'b0));
  _74ls245 _74ls245_1 (.DIR(1'b1), .nOE(nASSERT_ISRvHi), .A(ISRv_Hi[15:8]), .B(xfer[15:8]), .VCC(1'b1), .GND(1'b0));

  // Other names for the same wires on the sheet: xfer_hi[7:0] = xfer[15:8]; xfer_lo[7:0] = xfer[7:0]
endmodule
