// Digital circuit control_unit.dig as structural Verilog
module control_unit (
  input  nirq,
  input  [7:0] opcode,
  input  [7:0] flags,
  input  nreq,
  input  nrst,
  input  nnmi,
  input  clk,
  input  [15:0] nmi_addr,
  input  [15:0] irq_addr,
  input  addr_assert_int,
  input  [7:0] NMI_Op,
  input  [7:0] IRQ_Op,
  input  [7:0] REQ_Op,
  output [3:0] dbus_assert,
  output [4:0] dbus_load,
  output [3:0] alu_op,
  output [4:0] xfer_assert,
  output [2:0] xfer_load,
  output [2:0] addr_assert,
  output [2:0] count,
  output dec_sp,
  output nclk,
  output noffset,
  output rst,
  output [15:0] dbg,
  output [15:0] int_addr,
  output clr_ubr,
  output set_ubr,
  output set_sup,
  output set_nmi_inhib
);

  wire and_1_out, and_2_out, button_1_out, clk_t, clr_ext, m0, m1, nrst_useq, nset_ext, offset, rst_useq,
       seq_rst, sequencer_p1, sequencer_p4, sequencer_p5, sequencer_p6, set_ext;
  wire [1:0] Interrupt_Mode_m1;
  wire [7:0] Interrupt_Latch_q, ucode0_d, ucode1_d, ucode2_d, ucode3_d;
  wire [7:2] Mode_Latch_q;
  wire [7:5] _74ls273_4_q;
  wire [15:0] multiplexer_1_out;

  Button button_1 (.out(button_1_out));
  or or_1 (clk_t, button_1_out, clk);
  Multiplexer #(.Bits(16)) multiplexer_1 (.sel(m1), .in_0(nmi_addr), .in_1(irq_addr), .out(multiplexer_1_out));
  assign int_addr = ~addr_assert_int ? multiplexer_1_out : 16'bz;  // DriverInvSel driverinvsel_1
  not not_1 (nclk, clk_t);
  not not_2 (rst, nrst);
  not not_3 (noffset, offset);
  not not_4 (rst_useq, nrst_useq);
  not not_5 (set_ext, nset_ext);
  or or_2 (seq_rst, rst_useq, rst);
  and and_1 (and_1_out, dbg[0], dbg[1], dbg[2]);
  _74ls273 Interrupt_Latch (
    .CP(nclk), .nMR(nrst), .D({{5{1'b0}}, nirq, nnmi, nreq}), .VCC(1'b1), .GND(1'b0), .Q(Interrupt_Latch_q));
  or or_3 (clr_ext, seq_rst, and_1_out);
  mode_determination Interrupt_Mode (
    .nREQ(Interrupt_Latch_q[0]), .nNMI(Interrupt_Latch_q[1]), .nIRQ(Interrupt_Latch_q[2]),
    .NMI_Inhib(flags[7]), .IRQ_Enable(flags[0]), .M0(Interrupt_Mode_m1[0]), .M1(Interrupt_Mode_m1[1]));
  // _74193 sequencer: pin names not known; wires that end beside it: sequencer_p1, 1'b1, nclk, sequencer_p4, sequencer_p5, sequencer_p6, seq_rst, 1'b1, 1'b1, 1'b0, dbg[0], dbg[1], dbg[2]
  // NotConnected on sequencer_p1
  // NotConnected on sequencer_p4
  // NotConnected on sequencer_p5
  // NotConnected on sequencer_p6
  and and_2 (and_2_out, nclk, clr_ext);
  _74ls273 Mode_Latch (
    .CP(and_2_out), .nMR(nrst), .D({{6{1'b0}}, Interrupt_Mode_m1}), .VCC(1'b1), .GND(1'b0),
    .Q({Mode_Latch_q, m1, m0}));
  RS_FF_AS rs_ff_as_1 (.S(set_ext), .R(clr_ext), .Q(dbg[15]));  // open: nQ
  Multiplexer #(.Bits(8), .Selector_Bits(2)) multiplexer_2 (
    .sel({m1, m0}), .in_0(opcode), .in_1(NMI_Op), .in_2(IRQ_Op), .in_3(REQ_Op), .out(dbg[14:7]));
  ROM #(.AddrBits(16), .Bits(8)) ucode0 (
    .A({dbg[15:7], flags[1], flags[2], flags[3], flags[4], dbg[2:0]}), .sel(1'b1), .D(ucode0_d));
  ROM #(.AddrBits(16), .Bits(8)) ucode1 (
    .A({dbg[15:7], flags[1], flags[2], flags[3], flags[4], dbg[2:0]}), .sel(1'b1), .D(ucode1_d));
  ROM #(.AddrBits(16), .Bits(8)) ucode2 (
    .A({dbg[15:7], flags[1], flags[2], flags[3], flags[4], dbg[2:0]}), .sel(1'b1), .D(ucode2_d));
  ROM #(.AddrBits(16), .Bits(8)) ucode3 (
    .A({dbg[15:7], flags[1], flags[2], flags[3], flags[4], dbg[2:0]}), .sel(1'b1), .D(ucode3_d));
  _74ls273 _74ls273_1 (.CP(clk_t), .nMR(nrst), .D(ucode0_d), .VCC(1'b1), .GND(1'b0), .Q({alu_op, dbus_assert}));
  _74ls273 _74ls273_2 (.CP(clk_t), .nMR(nrst), .D(ucode1_d), .VCC(1'b1), .GND(1'b0), .Q({addr_assert, dbus_load}));
  _74ls273 _74ls273_3 (.CP(clk_t), .nMR(nrst), .D(ucode2_d), .VCC(1'b1), .GND(1'b0), .Q({xfer_load, xfer_assert}));
  _74ls273 _74ls273_4 (
    .CP(clk_t), .nMR(nrst), .D(ucode3_d), .VCC(1'b1), .GND(1'b0), .Q({_74ls273_4_q, offset, dec_sp, count}));
  // _74138 _74138_1: pin names not known; wires that end beside it: _74ls273_4_q[5], _74ls273_4_q[7], _74ls273_4_q[6], 1'b1, 1'b0, 1'b0, 1'b1, 1'b0, nrst_useq, nset_ext, set_ubr, clr_ubr, set_sup, set_nmi_inhib

  assign dbg[6:3] = {flags[1], flags[2], flags[3], flags[4]};

  // Other names for the same wires on the sheet: ucode_addr[15:0] = {dbg[15:7], flags[1], flags[2], flags[3], flags[4], dbg[2:0]};
  //   t_state[2:0] = dbg[2:0]; ext = dbg[15]; I_f = flags[0]; N_f = flags[1]; V_f = flags[2]; Z_f = flags[3];
  //   C_f = flags[4]; nmi_inhib = flags[7]; set_nmi = set_nmi_inhib

  // Notes on the sheet:
  //   nirq: default 1
  //   nreq: default 1
  //   nnmi: default 1
  //   nmi_addr: default 1
  //   irq_addr: default 1
  //   addr_assert_int: default 1
  //   NMI_Op: default 3
  //   IRQ_Op: default 4
  //   REQ_Op: default 2
  //   ucode0 loads microcode0.bin
  //   ucode1 loads microcode1.bin
  //   ucode2 loads microcode2.bin
  //   ucode3 loads microcode3.bin
endmodule
