// Digital circuit direct_page_register.dig as structural Verilog
module direct_page_register (
  input  [7:0] dbus,
  input  clk,
  input  clr,
  input  [7:0] rhs,
  input  [15:0] addr,
  input  assert_dp_addr,
  input  assert_t1_dbus,
  input  assert_t1_rhs,
  input  assert_dp_dbus,
  input  load_t1_dbus,
  input  load_dp_dbus,
  input  load_t2_dbus,
  input  assert_t_addr,
  input  assert_t2_dbus,
  input  assert_t2_lhs,
  input  t_inc,
  output [7:0] reg_dp,
  output [7:0] reg_t1,
  output [7:0] reg_t2
);

  wire assert_t1_addr, notconnected_1_out, notconnected_2_out, notconnected_3_out, notconnected_4_out,
       notconnected_5_out, notconnected_6_out, T1_hi_p3, T2_hi_p3, T2_lo_p3;
  wire [7:0] addr_hi, addr_lo, lhs;

  // _74ls173 DP_hi: pin names not known; wires that end beside it: dbus[7:4], 1'b1, 1'b0, clr, clk, load_dp_dbus, load_dp_dbus, 1'b0, 1'b0, reg_dp[7:4]
  // _74193 T2_hi: pin names not known; wires that end beside it: dbus[4], 1'b1, T2_hi_p3, dbus[5], dbus[6], dbus[7], clr, load_t2_dbus, 1'b1, 1'b0, reg_t2[4], reg_t2[5], reg_t2[6], reg_t2[7]
  _74ls245 DP_to_dbus (.DIR(1'b1), .nOE(assert_dp_dbus), .A(reg_dp), .B(dbus), .VCC(1'b1), .GND(1'b0));
  _74ls245 T1_to_dbus (.DIR(1'b1), .nOE(assert_t1_dbus), .A(reg_t1), .B(dbus), .VCC(1'b1), .GND(1'b0));
  _74ls245 T2_to_dbus (.DIR(1'b1), .nOE(assert_t2_dbus), .A(reg_t2), .B(dbus), .VCC(1'b1), .GND(1'b0));
  // _74ls173 DP_lo: pin names not known; wires that end beside it: dbus[3:0], 1'b1, 1'b0, clr, clk, load_dp_dbus, load_dp_dbus, 1'b0, 1'b0, reg_dp[3:0]
  // _74193 T2_lo: pin names not known; wires that end beside it: dbus[0], 1'b1, T2_lo_p3, dbus[1], dbus[2], dbus[3], clr, load_t2_dbus, 1'b1, 1'b0, T2_hi_p3, reg_t2[0], reg_t2[1], reg_t2[2], reg_t2[3]
  _74ls245 DP_to_addr_hi (.DIR(1'b1), .nOE(assert_dp_addr), .A(reg_dp), .B(addr_hi), .VCC(1'b1), .GND(1'b0));
  _74ls245 T1_to_addr_lo (.DIR(1'b1), .nOE(assert_t1_addr), .A(reg_t1), .B(addr_lo), .VCC(1'b1), .GND(1'b0));
  _74ls245 T2_to_addr_hi (.DIR(1'b1), .nOE(assert_t1_addr), .A(reg_t2), .B(addr_hi), .VCC(1'b1), .GND(1'b0));
  _74ls245 T1_to_rhs (.DIR(1'b1), .nOE(assert_t1_rhs), .A(reg_t1), .B(rhs), .VCC(1'b1), .GND(1'b0));
  _74ls245 T2_to_lhs (.DIR(1'b1), .nOE(assert_t2_lhs), .A(reg_t2), .B(lhs), .VCC(1'b1), .GND(1'b0));
  // _74193 T1_hi: pin names not known; wires that end beside it: dbus[4], 1'b1, T1_hi_p3, dbus[5], dbus[6], dbus[7], clr, load_t1_dbus, 1'b1, 1'b0, T2_lo_p3, reg_t1[4], reg_t1[5], reg_t1[6], reg_t1[7]
  // NotConnected on notconnected_1_out
  // NotConnected on notconnected_2_out
  // NotConnected on notconnected_3_out
  // NotConnected on notconnected_4_out
  // NotConnected on notconnected_5_out
  // NotConnected on notconnected_6_out
  // _7408 _7408_1: pin names not known; wires that end beside it: assert_dp_addr, assert_t_addr, notconnected_1_out, notconnected_2_out, notconnected_3_out, notconnected_4_out, notconnected_5_out, notconnected_6_out, 1'b1, 1'b0, assert_t1_addr
  // _74193 T1_lo: pin names not known; wires that end beside it: dbus[0], 1'b1, t_inc, dbus[1], dbus[2], dbus[3], clr, load_t1_dbus, 1'b1, 1'b0, T1_hi_p3, reg_t1[0], reg_t1[1], reg_t1[2], reg_t1[3]

  // Other names for the same wires on the sheet: q_t2[7:0] = reg_t2; q_t2_hi[3:0] = reg_t2[7:4];
  //   q_t2_lo[3:0] = reg_t2[3:0]; q_t1[7:0] = reg_t1; q_t1_hi[3:0] = reg_t1[7:4]; q_t1_lo[3:0] = reg_t1[3:0];
  //   d_0 = dbus[0]; d_lo[3:0] = dbus[3:0]; d_1 = dbus[1]; d_2 = dbus[2]; d_3 = dbus[3]; d_4 = dbus[4];
  //   d_hi[3:0] = dbus[7:4]; d_5 = dbus[5]; d_6 = dbus[6]; d_7 = dbus[7]; q_dp[7:0] = reg_dp;
  //   q_dp_hi[3:0] = reg_dp[7:4]; q_dp_lo[3:0] = reg_dp[3:0]

  // Notes on the sheet:
  //   assert_dp_addr: default 1
  //   assert_t1_dbus: default 1
  //   assert_t1_rhs: default 1
  //   assert_dp_dbus: default 1
  //   load_t1_dbus: default 1
  //   load_dp_dbus: default 1
  //   load_t2_dbus: default 1
  //   assert_t_addr: default 1
  //   assert_t2_dbus: default 1
  //   assert_t2_lhs: default 1
endmodule
