// Digital circuit general_purpose_register.dig as structural Verilog
module general_purpose_register (
  input  clk,
  input  dbus_load,
  input  dbus_assert,
  input  lhs_assert,
  input  rhs_assert,
  input  clr,
  input  [7:0] dbus,
  output [7:0] lhs,
  output [7:0] rhs,
  output [7:0] \reg 
);

  // _74ls173 _74ls173_1: pin names not known; wires that end beside it: dbus[7:4], 1'b1, 1'b0, clr, clk, dbus_load, dbus_load, 1'b0, 1'b0, \reg [7:4]
  _74ls245 to_dbus (.DIR(1'b1), .nOE(dbus_assert), .A(\reg ), .B(dbus), .VCC(1'b1), .GND(1'b0));
  // _74ls173 _74ls173_2: pin names not known; wires that end beside it: dbus[3:0], 1'b1, 1'b0, clr, clk, dbus_load, dbus_load, 1'b0, 1'b0, \reg [3:0]
  _74ls245 to_lhs (.DIR(1'b1), .nOE(lhs_assert), .A(\reg ), .B(lhs), .VCC(1'b1), .GND(1'b0));
  _74ls245 to_rhs (.DIR(1'b1), .nOE(rhs_assert), .A(\reg ), .B(rhs), .VCC(1'b1), .GND(1'b0));

  // Other names for the same wires on the sheet: dbus_lo[3:0] = dbus[3:0]; dbus_hi[3:0] = dbus[7:4]; q[7:0] = \reg ;
  //   q_hi[3:0] = \reg [7:4]; q_lo[3:0] = \reg [3:0]

  // Notes on the sheet:
  //   dbus_load: default 1
  //   dbus_assert: default 1
  //   lhs_assert: default 1
  //   rhs_assert: default 1
endmodule
