// Digital circuit gpr_pair.dig as structural Verilog
module gpr_pair (
  input  addr_assert,
  input  xfer_load,
  input  a_dbus_load,
  input  b_dbus_load,
  input  a_dbus_assert,
  input  b_dbus_assert,
  input  a_lhs_assert,
  input  b_lhs_assert,
  input  a_rhs_assert,
  input  b_rhs_assert,
  input  [7:0] dbus,
  input  [15:0] xfer,
  input  nclr,
  output [15:0] addr,
  output [7:0] reg_hi,
  output [7:0] reg_lo
);

  wire load_b, load_control_p5, load_control_p6, load_control_p7, load_control_p8, load_hi, load_hi_dbus,
       load_hi_t, load_lo, load_lo_dbus;
  wire [3:0] d_00, d_01, d_10, d_11;
  wire [7:0] addr_hi_t, addr_lo_t, d_hi, d_lo, q_a, q_b;

  // _7408 load_control: pin names not known; wires that end beside it: xfer_load, load_hi_dbus, xfer_load, load_lo_dbus, load_control_p5, load_control_p6, load_control_p7, load_control_p8, 1'b1, 1'b0, load_hi_t, load_b
  // NotConnected on load_control_p5
  // NotConnected on load_control_p6
  // NotConnected on load_control_p7
  // NotConnected on load_control_p8
  _74ls157 Hi_Reg_Hi_mux_in (
    .S(load_hi_dbus), .A(dbus[7:4]), .B(xfer[15:12]), .G(1'b0), .VCC(1'b1), .GND(1'b0), .Y(d_11));
  _74ls273 Hi_Reg (.CP(load_hi), .nMR(nclr), .D(d_hi), .VCC(1'b1), .GND(1'b0), .Q(reg_hi));
  _74ls245 Hi_Reg_to_dbus (.DIR(1'b1), .nOE(a_dbus_assert), .A(q_a), .B(dbus), .VCC(1'b1), .GND(1'b0));
  _74ls245 Hi_Reg_to_rhs (.DIR(1'b1), .nOE(a_rhs_assert), .A(q_a), .B(xfer[7:0]), .VCC(1'b1), .GND(1'b0));
  _74ls273 Lo_Reg (.CP(load_lo), .nMR(nclr), .D(d_lo), .VCC(1'b1), .GND(1'b0), .Q(reg_lo));
  _74ls157 Hi_Reg_Lo_mux_in (
    .S(load_hi_dbus), .A(dbus[3:0]), .B(xfer[11:8]), .G(1'b0), .VCC(1'b1), .GND(1'b0), .Y(d_10));
  _74ls245 Hi_Reg_to_lhs (.DIR(1'b1), .nOE(a_lhs_assert), .A(q_a), .B(xfer[15:8]), .VCC(1'b1), .GND(1'b0));
  _74ls245 Hi_Reg_to_addr (.DIR(1'b1), .nOE(addr_assert), .A(q_a), .B(addr_hi_t), .VCC(1'b1), .GND(1'b0));
  _74ls157 Lo_Reg_Hi_mux_in (
    .S(load_lo_dbus), .A(dbus[7:4]), .B(xfer[7:4]), .G(1'b0), .VCC(1'b1), .GND(1'b0), .Y(d_01));
  _74ls245 Lo_Reg_to_dbus (.DIR(1'b1), .nOE(b_dbus_assert), .A(q_b), .B(dbus), .VCC(1'b1), .GND(1'b0));
  _74ls245 Lo_Reg_to_rhs (.DIR(1'b1), .nOE(b_rhs_assert), .A(q_b), .B(xfer[7:0]), .VCC(1'b1), .GND(1'b0));
  _74ls157 Lo_Reg_Lo_mux_in (
    .S(load_lo_dbus), .A(dbus[3:0]), .B(xfer[3:0]), .G(1'b0), .VCC(1'b1), .GND(1'b0), .Y(d_00));
  _74ls245 Lo_Reg_to_lhs (.DIR(1'b1), .nOE(b_lhs_assert), .A(q_b), .B(xfer[15:8]), .VCC(1'b1), .GND(1'b0));
  _74ls245 Lo_Reg_to_addr (.DIR(1'b1), .nOE(addr_assert), .A(q_b), .B(addr_lo_t), .VCC(1'b1), .GND(1'b0));

  // Other names for the same wires on the sheet: addr_hi[7:0] = addr[15:8]; addr_lo[7:0] = addr[7:0];
  //   assert_a_dbus = a_dbus_assert; assert_a_lhs = a_lhs_assert; assert_a_rhs = a_rhs_assert;
  //   assert_addr = addr_assert; assert_b_dbus = b_dbus_assert; assert_b_lhs = b_lhs_assert;
  //   assert_b_rhs = b_rhs_assert; d_lo_t[7:0] = {d_01, d_00}; d_hi_t[7:0] = {d_11, d_10}; dbus_lo[3:0] = dbus[3:0];
  //   dbus_hi[3:0] = dbus[7:4]; lhs[7:0] = xfer[15:8]; xfer_10[3:0] = xfer[11:8]; xfer_11[3:0] = xfer[15:12];
  //   load_a_dbus = a_dbus_load; load_b_dbus = b_dbus_load; load_xfer = xfer_load; q_hi[7:0] = reg_hi;
  //   q_lo[7:0] = reg_lo; rhs[7:0] = xfer[7:0]; xfer_00[3:0] = xfer[3:0]; xfer_01[3:0] = xfer[7:4]

  // Notes on the sheet:
  //   addr_assert: default 1
  //   xfer_load: default 1
  //   a_dbus_load: default 1
  //   b_dbus_load: default 1
  //   a_dbus_assert: default 1
  //   b_dbus_assert: default 1
  //   a_lhs_assert: default 1
  //   b_lhs_assert: default 1
  //   a_rhs_assert: default 1
  //   b_rhs_assert: default 1
endmodule
