// Digital circuit instruction_register.dig as structural Verilog
module instruction_register (
  input  clk,
  input  [7:0] dbus,
  input  dbus_load,
  input  clr,
  output [7:0] opcode
);

  // _74ls173 high: pin names not known; wires that end beside it: dbus[7:4], 1'b1, 1'b0, clr, clk, dbus_load, dbus_load, 1'b0, 1'b0, opcode[7:4]
  // _74ls173 lo: pin names not known; wires that end beside it: dbus[3:0], 1'b1, 1'b0, clr, clk, dbus_load, dbus_load, 1'b0, 1'b0, opcode[3:0]

  // Other names for the same wires on the sheet: dbus_lo[3:0] = dbus[3:0]; dbus_hi[3:0] = dbus[7:4]; load = dbus_load;
  //   q[7:0] = opcode; q_hi[3:0] = opcode[7:4]; q_lo[3:0] = opcode[3:0]
endmodule
