// Digital circuit triple_clock.dig as structural Verilog
module triple_clock (
  input  nrun,
  input  ndemo,
  input  nbreak,
  input  crystal,
  input  _555,
  input  step,
  input  nbrk,
  input  nrun_rst,
  input  ndemo_rst,
  input  nstep_rst,
  output clk_cpu,
  output clk_crystal
);

  wire _74574_1_p13, _74574_1_p14, _74574_1_p15, and_1_out, and_2_out, and_3_out, nand_1_out, nand_2_out,
       nand_3_out;

  nand nand_1 (nand_1_out, and_2_out, and_3_out);
  nand nand_2 (nand_2_out, and_1_out, and_3_out);
  nand nand_3 (nand_3_out, and_1_out, and_2_out);
  and and_1 (and_1_out, nand_1_out, nrun_rst, nrun);
  and and_2 (and_2_out, nand_2_out, ndemo_rst, ndemo);
  and and_3 (and_3_out, nstep_rst, nand_3_out, nbreak, nbrk);
  // _74574 _74574_1: pin names not known; wires that end beside it: 1'b0, crystal, and_3_out, and_1_out, and_2_out, 1'b0, 1'b0, 1'b0, 1'b0, 1'b0, 1'b1, 1'b0, _74574_1_p13, _74574_1_p14, _74574_1_p15
  // _74151 _74151_1: pin names not known; wires that end beside it: _74574_1_p13, _74574_1_p14, _74574_1_p15, 1'b0, step, step, step, crystal, step, _555, step, step, 1'b1, 1'b0, clk_cpu

  assign clk_crystal = crystal;

  // Other names for the same wires on the sheet: clk_demo = _555; clk_step = step

  // Notes on the sheet:
  //   nrun: default 1
  //   ndemo: default 1
  //   crystal: Hz: 5
endmodule
